// Logisim project Cache Direta.circ as structural Verilog: 37 circuits, main circuit Circuito Principal
// Regist
module Registrador (
  input  [15:0] Entrada,
  input  Clock,
  input  RESET,
  input  Enable,
  output [15:0] \Saída 
);

  D_Flip_Flop d_ff_1 (.clk(Clock), .D(Entrada[8]), .Q(\Saída [8]), .en(Enable), .reset(RESET));  // open: Qn, preset
  D_Flip_Flop d_ff_2 (.clk(Clock), .D(Entrada[9]), .Q(\Saída [9]), .en(Enable), .reset(RESET));  // open: Qn, preset
  D_Flip_Flop d_ff_3 (.clk(Clock), .D(Entrada[10]), .Q(\Saída [10]), .en(Enable), .reset(RESET));  // open: Qn, preset
  D_Flip_Flop d_ff_4 (.clk(Clock), .D(Entrada[11]), .Q(\Saída [11]), .en(Enable), .reset(RESET));  // open: Qn, preset
  D_Flip_Flop d_ff_5 (.clk(Clock), .D(Entrada[12]), .Q(\Saída [12]), .en(Enable), .reset(RESET));  // open: Qn, preset
  D_Flip_Flop d_ff_6 (.clk(Clock), .D(Entrada[13]), .Q(\Saída [13]), .en(Enable), .reset(RESET));  // open: Qn, preset
  D_Flip_Flop d_ff_7 (.clk(Clock), .D(Entrada[14]), .Q(\Saída [14]), .en(Enable), .reset(RESET));  // open: Qn, preset
  D_Flip_Flop d_ff_8 (.clk(Clock), .D(Entrada[15]), .Q(\Saída [15]), .en(Enable), .reset(RESET));  // open: Qn, preset
  D_Flip_Flop d_ff_9 (.clk(Clock), .D(Entrada[0]), .Q(\Saída [0]), .en(Enable), .reset(RESET));  // open: Qn, preset
  D_Flip_Flop d_ff_10 (.clk(Clock), .D(Entrada[1]), .Q(\Saída [1]), .en(Enable), .reset(RESET));  // open: Qn, preset
  D_Flip_Flop d_ff_11 (.clk(Clock), .D(Entrada[2]), .Q(\Saída [2]), .en(Enable), .reset(RESET));  // open: Qn, preset
  D_Flip_Flop d_ff_12 (.clk(Clock), .D(Entrada[3]), .Q(\Saída [3]), .en(Enable), .reset(RESET));  // open: Qn, preset
  D_Flip_Flop d_ff_13 (.clk(Clock), .D(Entrada[4]), .Q(\Saída [4]), .en(Enable), .reset(RESET));  // open: Qn, preset
  D_Flip_Flop d_ff_14 (.clk(Clock), .D(Entrada[5]), .Q(\Saída [5]), .en(Enable), .reset(RESET));  // open: Qn, preset
  D_Flip_Flop d_ff_15 (.clk(Clock), .D(Entrada[6]), .Q(\Saída [6]), .en(Enable), .reset(RESET));  // open: Qn, preset
  D_Flip_Flop d_ff_16 (.clk(Clock), .D(Entrada[7]), .Q(\Saída [7]), .en(Enable), .reset(RESET));  // open: Qn, preset
endmodule

module Processador (
  input  Reset,
  input  Cache_Miss_Load,
  input  [15:0] \Instrução ,
  input  Cache_Miss,
  input  [15:0] Entrada_Dado_Load,
  input  Clock_Fonte,
  output [15:0] \Saída_ULA_L_S ,
  output [15:0] \Saída_2_Banco ,
  output Pre_store,
  output Ciclo_Posterior_ao_Store,
  output Primeiro_Ciclo,
  output Load,
  output Store,
  output [15:0] \Saída_PC_Atual ,
  output Clock,
  output Fim_do_Programa
);

  wire and_2_out, and_3_out, and_4_out, and_5_out, and_6_out, and_7_out, and_8_out, Branch, Desvio,
       Fim_do_Load, gerenciador_clock_inicial_1_clock_inicial, Imdediato, Jump, Load_t, Ocorreu_Cache_Miss,
       Ocorreu_Cache_Miss_Dado_Load, or_1_out, or_2_out, or_3_out, Reg_Write, Sinal_Funct, Store_t, Zero_ULA;
  wire [2:0] D___Reg__Fonte_2, Funct, I___Reg__Destino, multiplexer_4_out, multiplexer_8_out,
       multiplexer_9_out, Opcode, R___Reg__Destino, R___Reg__Fonte_2;
  wire [3:0] D___Reg__Fonte_1, I___Reg__Fonte_1, multiplexer_6_out, multiplexer_7_out, Operation_ALU,
       R___Reg__Fonte_1, selecionar_funct_ou_operation_1_out_4;
  wire [5:0] divisor_de_campos_1_i_constante;
  wire [6:0] divisor_de_campos_1_d___imediato;
  wire [12:0] \J_Endereço ;
  wire [15:0] calcular_desvio_1_end__branch, \concatenar_jump_1_endereço_final , \D___Endereço , \Endereço ,
       I_Constante, \Instrução_t , \Lê_Dado_A , multiplexer_2_out, multiplexer_5_out, multiplexer_10_out,
       multiplexer_11_out, PC___1;

  Multiplexer #(.width(16)) multiplexer_1 (
    .in0(PC___1), .in1(multiplexer_2_out), .out(\Endereço ), .sel(or_1_out));  // open: en
  or or_1 (or_1_out, Desvio, Jump);
  Multiplexer #(.width(16)) multiplexer_2 (
    .in0(calcular_desvio_1_end__branch), .in1(\concatenar_jump_1_endereço_final ), .out(multiplexer_2_out),
    .sel(Jump));  // open: en
  PC pc_1 (
    .\Endereço (\Endereço ), .Reset(Reset), .Clock(Clock), .Branch(Desvio), .PC_Atual(\Saída_PC_Atual ),
    .Cache_Miss(Cache_Miss), .Cache_Miss_Load(Cache_Miss_Load), .Load(Load_t),
    .Ocorreu_Cache_Miss_Load(Ocorreu_Cache_Miss_Dado_Load), .Fim_do_Load(Fim_do_Load),
    .Ocorreu_Cache_Miss(Ocorreu_Cache_Miss), .Pre_store(Pre_store),
    .Ciclo_Posterior_ao_Store(Ciclo_Posterior_ao_Store));
  Calcular_Desvio calcular_desvio_1 (
    .\Próx__End (PC___1), .\I_Constante_ou_Endereço (\D___Endereço ),
    .End__Branch(calcular_desvio_1_end__branch));
  Concatenar_Jump concatenar_jump_1 (
    .Jump(\J_Endereço ), .PC_atual(PC___1), .\Endereço_Final (\concatenar_jump_1_endereço_final ));
  Adder #(.width(16)) adder_1 (.a(16'h1), .b(\Saída_PC_Atual ), .out(PC___1));  // open: cin, cout
  Multiplexer multiplexer_3 (.in0(Clock_Fonte), .in1(1'b1), .out(Clock), .sel(Fim_do_Programa));  // open: en
  Unidade_de_Controle unidade_de_controle_1 (
    .out_2(Operation_ALU), .Opcode(Opcode), .REG_WRITE(Reg_Write), .BRANCH(Branch), .IMMEDIATE(Imdediato),
    .JUMP(Jump), .STORE(Store_t), .LOAD(Load_t), .FUNCT(Sinal_Funct));
  Divisor_de_Campos divisor_de_campos_1 (
    .Entrada(\Instrução_t ), .I_Constante(divisor_de_campos_1_i_constante),
    .\J_Endereço_ou_Registrador (\J_Endereço ), .I___Reg__Fonte_1(I___Reg__Fonte_1),
    .I___Reg__Destino(I___Reg__Destino), .D___Reg__Fonte_2(D___Reg__Fonte_2),
    .D___Imediato(divisor_de_campos_1_d___imediato), .D___Reg__Fonte_1(D___Reg__Fonte_1),
    .R___Reg__Fonte_2(R___Reg__Fonte_2), .R___Reg__Destino(R___Reg__Destino), .Funct(Funct), .Opcode(Opcode),
    .R___Reg__Fonte_1(R___Reg__Fonte_1));
  Cache_Miss_Load_Handler cache_miss_load_handler_1 (
    .Clock(Clock), .Cache_Miss_Load(Cache_Miss_Load), .Load(Load_t), .PC_Atual(\Saída_PC_Atual ),
    .\Entrada_Instrução (\Instrução ), .Primeiro_Ciclo(Primeiro_Ciclo), .\Instrução (\Instrução_t ),
    .Cache_Miss(Cache_Miss), .Ocorreu_Cache_Miss_Dado_Load(Ocorreu_Cache_Miss_Dado_Load),
    .Fim_do_Load(Fim_do_Load), .Ocorreu_Cache_Miss(Ocorreu_Cache_Miss),
    .Ciclo_Posterior_ao_Store(Ciclo_Posterior_ao_Store));
  assign \D___Endereço  = {{9{1'b0}}, divisor_de_campos_1_d___imediato};  // Bit_Extender bit_extender_1
  assign I_Constante = {{10{1'b0}}, divisor_de_campos_1_i_constante};  // Bit_Extender bit_extender_2
  Multiplexer #(.width(3)) multiplexer_4 (
    .in0(R___Reg__Fonte_2), .in1(I___Reg__Destino), .out(multiplexer_4_out), .sel(Store_t));  // open: en
  and and_1 (Desvio, Zero_ULA, Branch);
  Multiplexer #(.width(16)) multiplexer_5 (
    .in0(\Saída_2_Banco ), .in1(I_Constante), .out(multiplexer_5_out), .sel(Imdediato));  // open: en
  Multiplexer #(.width(4)) multiplexer_6 (
    .in0(R___Reg__Fonte_1), .in1(I___Reg__Fonte_1), .out(multiplexer_6_out), .sel(Imdediato));  // open: en
  Multiplexer #(.width(4)) multiplexer_7 (
    .in0(multiplexer_6_out), .in1(D___Reg__Fonte_1), .out(multiplexer_7_out), .sel(Branch));  // open: en
  Multiplexer #(.width(3)) multiplexer_8 (
    .in0(multiplexer_4_out), .in1(D___Reg__Fonte_2), .out(multiplexer_8_out), .sel(Branch));  // open: en
  Multiplexer #(.width(3)) multiplexer_9 (
    .in0(R___Reg__Destino), .in1(I___Reg__Destino), .out(multiplexer_9_out), .sel(Imdediato));  // open: en
  and and_2 (and_2_out, Store_t, ~Cache_Miss);  // AND_Gate
  \Unidade_Lógica_e_Aritmética  \unidade_lógica_e_aritmética_1  (
    .Funct(selecionar_funct_ou_operation_1_out_4), .Entrada_A(\Lê_Dado_A ), .Entrada_B(multiplexer_5_out),
    .\Saída (\Saída_ULA_L_S ), .Zero(Zero_ULA));
  Store_Handler store_handler_1 (
    .Store(and_2_out), .Clock(Clock), .\Pré_store (Pre_store),
    .Ciclo_Posterior_ao_Store(Ciclo_Posterior_ao_Store));
  Selecionar_Funct_ou_Operation selecionar_funct_ou_operation_1 (
    .out_4(selecionar_funct_ou_operation_1_out_4), .Operation_ALU(Operation_ALU), .Opcode(Funct),
    .Sinal_Funct(Sinal_Funct));
  Banco_de_Registradores banco_de_registradores_1 (
    .Reg__Escrita(multiplexer_9_out), .Entrada(multiplexer_10_out), .\Saída_de_Dados_1 (\Lê_Dado_A ),
    .\Saída_de_Dados_2 (\Saída_2_Banco ), .RESET(Reset), .Reg__Leitura_1(multiplexer_7_out),
    .Reg__Leitura_2(multiplexer_8_out), .Cache_Miss(Cache_Miss), .Clock(and_4_out), .in_7(\Saída_PC_Atual ),
    .Enable(and_3_out));
  and and_3 (and_3_out, ~Clock, Reg_Write);  // AND_Gate
  and and_4 (and_4_out, ~gerenciador_clock_inicial_1_clock_inicial, ~Cache_Miss, Reg_Write);  // AND_Gate
  Multiplexer #(.width(16)) multiplexer_10 (
    .in0(multiplexer_11_out), .out(multiplexer_10_out), .sel(or_2_out));  // open: in1, en
  or or_2 (or_2_out, Cache_Miss_Load, Cache_Miss);
  Multiplexer #(.width(16)) multiplexer_11 (
    .in0(\Saída_ULA_L_S ), .in1(Entrada_Dado_Load), .out(multiplexer_11_out), .sel(Load_t));  // open: en
  Gerenciador_Clock_Inicial gerenciador_clock_inicial_1 (
    .Clock_Inicial(gerenciador_clock_inicial_1_clock_inicial), .Clock(Clock), .PC_Atual(\Saída_PC_Atual ));
  and and_5 (and_5_out, Fim_do_Load, ~Load_t, Clock);  // AND_Gate
  and and_6 (and_6_out, Fim_do_Load, Cache_Miss);
  and and_7 (and_7_out, Store_t, ~Cache_Miss);  // AND_Gate
  and and_8 (and_8_out, Pre_store, ~Ciclo_Posterior_ao_Store);  // AND_Gate
  Gerenciador_Clock gerenciador_clock_1 (
    .Clock(Clock), .Cache_Miss(Cache_Miss), .\Saída_PC_Atual (\Saída_PC_Atual ), .\Saída_Cache (\Instrução ),
    .Fim_do_Programa(Fim_do_Programa));
  Multiplexer multiplexer_12 (.in0(Load_t), .in1(1'b0), .out(Load), .sel(or_3_out));  // open: en
  or or_3 (or_3_out, and_5_out, Ocorreu_Cache_Miss, and_6_out);
  and and_9 (Store, and_7_out, ~and_8_out);  // AND_Gate

  // Other names for the same wires on the sheet: Instrução_Entrada[15:0] = \Instrução ;
  //   Lê_Dado_B[15:0] = \Saída_2_Banco ; PC_Atual[15:0] = \Saída_PC_Atual ; Pré_store = Pre_store;
  //   Saída_ULA[15:0] = \Saída_ULA_L_S 
endmodule

// Div. Campos
module Divisor_de_Campos (
  input  [15:0] Entrada,
  output [2:0] Funct,
  output [2:0] R___Reg__Fonte_2,
  output [5:0] I_Constante,
  output [3:0] R___Reg__Fonte_1,
  output [12:0] \J_Endereço_ou_Registrador ,
  output [3:0] I___Reg__Fonte_1,
  output [2:0] R___Reg__Destino,
  output [2:0] I___Reg__Destino,
  output [2:0] Opcode,
  output [6:0] D___Imediato,
  output [2:0] D___Reg__Fonte_2,
  output [3:0] D___Reg__Fonte_1
);


  assign D___Imediato = Entrada[6:0];
  assign D___Reg__Fonte_1 = {1'b0, Entrada[12:10]};
  assign D___Reg__Fonte_2 = Entrada[9:7];
  assign Funct = Entrada[2:0];
  assign I___Reg__Destino = Entrada[12:10];
  assign I___Reg__Fonte_1 = Entrada[9:6];
  assign I_Constante = Entrada[5:0];
  assign \J_Endereço_ou_Registrador  = Entrada[12:0];
  assign Opcode = Entrada[15:13];
  assign R___Reg__Destino = Entrada[12:10];
  assign R___Reg__Fonte_1 = Entrada[9:6];
  assign R___Reg__Fonte_2 = Entrada[5:3];

  // Other names for the same wires on the sheet: Palavra[15:0] = Entrada
endmodule

// B. Regist
module Banco_de_Registradores (
  input  Cache_Miss,
  input  Clock,
  input  [3:0] Reg__Leitura_1,
  input  [2:0] Reg__Leitura_2,
  input  [2:0] Reg__Escrita,
  input  [15:0] Entrada,
  input  [15:0] in_7,
  input  RESET,
  input  Enable,
  output [15:0] \Saída_de_Dados_1 ,
  output [15:0] \Saída_de_Dados_2 
);

  wire and_1_out, and_2_out, and_3_out, and_4_out, and_5_out, and_6_out, and_7_out, and_8_out,
       clock_leitura_banco, Clock_Negado, Clock_t, comparator_1_eq, multiplexer_1_out, reg_banco_1,
       reg_banco_2, reg_banco_3, reg_banco_4, reg_banco_5, reg_banco_6, reg_banco_7, reg_banco_8;
  wire [15:0] \input_end_inicio_programa_1_end__início_do_programa , \r1_saída , \r2_saída , \r3_saída ,
       \r4_saída , \r5_saída , \r6_saída , \r7_saída , \r8_saída , \rb_saída ;

  Decoder #(.select(3)) decoder_1 (
    .out0(reg_banco_1), .out1(reg_banco_2), .out2(reg_banco_3), .out3(reg_banco_4), .out4(reg_banco_5),
    .out5(reg_banco_6), .out6(reg_banco_7), .out7(reg_banco_8), .sel(Reg__Escrita));  // open: en
  not not_1 (Clock_Negado, Clock);
  Comparator #(.width(16)) comparator_1 (
    .a(in_7), .b(\input_end_inicio_programa_1_end__início_do_programa ), .eq(comparator_1_eq));  // open: gt, lt
  Input_End__Inicio_Programa input_end_inicio_programa_1 (.\End__Início_do_Programa (\input_end_inicio_programa_1_end__início_do_programa ));
  Multiplexer multiplexer_1 (.in0(Clock_t), .in1(1'b0), .out(multiplexer_1_out), .sel(Cache_Miss));  // open: en
  Multiplexer multiplexer_2 (.in0(Clock), .in1(Clock_Negado), .out(Clock_t), .sel(comparator_1_eq));  // open: en
  not not_2 (clock_leitura_banco, multiplexer_1_out);
  and and_1 (and_1_out, reg_banco_1, multiplexer_1_out);
  and and_2 (and_2_out, reg_banco_2, multiplexer_1_out);
  and and_3 (and_3_out, reg_banco_3, multiplexer_1_out);
  and and_4 (and_4_out, reg_banco_4, multiplexer_1_out);
  and and_5 (and_5_out, reg_banco_5, multiplexer_1_out);
  and and_6 (and_6_out, reg_banco_6, multiplexer_1_out);
  and and_7 (and_7_out, reg_banco_7, multiplexer_1_out);
  and and_8 (and_8_out, reg_banco_8, multiplexer_1_out);
  Registrador r1 (.Entrada(Entrada), .Clock(and_1_out), .RESET(RESET), .\Saída (\r1_saída ), .Enable(Enable));
  Registrador r2 (.Entrada(Entrada), .Clock(and_2_out), .RESET(RESET), .\Saída (\r2_saída ), .Enable(Enable));
  Registrador r3 (.Entrada(Entrada), .Clock(and_3_out), .RESET(RESET), .\Saída (\r3_saída ), .Enable(Enable));
  Registrador r4 (.Entrada(Entrada), .Clock(and_4_out), .RESET(RESET), .\Saída (\r4_saída ), .Enable(Enable));
  Registrador r5 (.Entrada(Entrada), .Clock(and_5_out), .RESET(RESET), .\Saída (\r5_saída ), .Enable(Enable));
  Registrador r6 (.Entrada(Entrada), .Clock(and_6_out), .RESET(RESET), .\Saída (\r6_saída ), .Enable(Enable));
  Registrador r7 (.Entrada(Entrada), .Clock(and_7_out), .RESET(RESET), .\Saída (\r7_saída ), .Enable(Enable));
  Registrador r8 (.Entrada(Entrada), .Clock(and_8_out), .RESET(RESET), .\Saída (\r8_saída ), .Enable(Enable));
  Registrador rb (
    .Entrada({16{1'b0}}), .Clock(multiplexer_1_out), .RESET(RESET), .\Saída (\rb_saída ));  // open: Enable
  Multiplexer #(.select(4), .width(16)) multiplexer_3 (
    .in0(\r1_saída ), .in1(\r2_saída ), .in2(\r3_saída ), .in3(\r4_saída ), .in4(\r5_saída ),
    .in5(\r6_saída ), .in6(\r7_saída ), .in7(\r8_saída ), .in8(\rb_saída ), .out(\Saída_de_Dados_1 ),
    .sel(Reg__Leitura_1));  // open: in9, in10, in11, in12, in13, in14, in15, en
  Multiplexer #(.select(3), .width(16)) multiplexer_4 (
    .in0(\r1_saída ), .in1(\r2_saída ), .in2(\r3_saída ), .in3(\r4_saída ), .in4(\r5_saída ),
    .in5(\r6_saída ), .in6(\r7_saída ), .in7(\r8_saída ), .out(\Saída_de_Dados_2 ), .sel(Reg__Leitura_2));  // open: en

  // Other names for the same wires on the sheet: Clock_Fonte = Clock; PC_Atual[15:0] = in_7
endmodule

// Regist
module Registrador_Zero (
  output [15:0] \Saída 
);

  D_Flip_Flop d_ff_1 (.Q(\Saída [15]));  // open: clk, D, Qn, preset, en, reset
  D_Flip_Flop d_ff_2 (.Q(\Saída [14]));  // open: clk, D, Qn, preset, en, reset
  D_Flip_Flop d_ff_3 (.Q(\Saída [13]));  // open: clk, D, Qn, preset, en, reset
  D_Flip_Flop d_ff_4 (.Q(\Saída [12]));  // open: clk, D, Qn, preset, en, reset
  D_Flip_Flop d_ff_5 (.Q(\Saída [11]));  // open: clk, D, Qn, preset, en, reset
  D_Flip_Flop d_ff_6 (.Q(\Saída [10]));  // open: clk, D, Qn, preset, en, reset
  D_Flip_Flop d_ff_7 (.Q(\Saída [9]));  // open: clk, D, Qn, preset, en, reset
  D_Flip_Flop d_ff_8 (.Q(\Saída [8]));  // open: clk, D, Qn, preset, en, reset
  D_Flip_Flop d_ff_9 (.Q(\Saída [7]));  // open: clk, D, Qn, preset, en, reset
  D_Flip_Flop d_ff_10 (.Q(\Saída [6]));  // open: clk, D, Qn, preset, en, reset
  D_Flip_Flop d_ff_11 (.Q(\Saída [5]));  // open: clk, D, Qn, preset, en, reset
  D_Flip_Flop d_ff_12 (.Q(\Saída [4]));  // open: clk, D, Qn, preset, en, reset
  D_Flip_Flop d_ff_13 (.Q(\Saída [3]));  // open: clk, D, Qn, preset, en, reset
  D_Flip_Flop d_ff_14 (.Q(\Saída [2]));  // open: clk, D, Qn, preset, en, reset
  D_Flip_Flop d_ff_15 (.Q(\Saída [1]));  // open: clk, D, Qn, preset, en, reset
  D_Flip_Flop d_ff_16 (.Q(\Saída [0]));  // open: clk, D, Qn, preset, en, reset
endmodule

// ULA
module \Unidade_Lógica_e_Aritmética  (
  input  [3:0] Funct,
  input  [15:0] Entrada_A,
  input  [15:0] Entrada_B,
  output Zero,
  output [15:0] \Saída 
);

  wire and_2_out, and_3_out, and_4_out, and_5_out, comparator_2_eq, comparator_3_eq, comparator_4_eq,
       resultado_beq, resultado_bne;
  wire [3:0] bitselector_1_out, bitselector_2_out;
  wire [15:0] \and , \nand , \nor , operando_1_add, operando_1_and, operando_1_bne, operando_1_nand,
       operando_1_nor, operando_1_or, operando_1_sll, operando_1_srl, operando_1_sub, operando_1beq,
       operando_2_add, operando_2_and, operando_2_beq, operando_2_bne, operando_2_nand, operando_2_nor,
       operando_2_or, operando_2_sll, operando_2_srl, operando_2_sub, \or , shift_left, shift_right, soma,
       subtracao;

  Demultiplexer #(.select(4), .width(16)) demultiplexer_1 (
    .out0(operando_1_add), .out1(operando_1_sub), .out2(operando_1_and), .out3(operando_1_or),
    .out4(operando_1_nand), .out5(operando_1_nor), .out6(operando_1_sll), .out7(operando_1_srl),
    .out8(operando_1beq), .out9(operando_1_bne), .in(Entrada_A), .sel(Funct));  // open: out10, out11, out12, out13, out14, out15, en
  Demultiplexer #(.select(4), .width(16)) demultiplexer_2 (
    .out0(operando_2_add), .out1(operando_2_sub), .out2(operando_2_and), .out3(operando_2_or),
    .out4(operando_2_nand), .out5(operando_2_nor), .out6(operando_2_sll), .out7(operando_2_srl),
    .out8(operando_2_beq), .out9(operando_2_bne), .in(Entrada_B), .sel(Funct));  // open: out10, out11, out12, out13, out14, out15, en
  Adder #(.width(16)) adder_1 (.a(operando_1_add), .b(operando_2_add), .out(soma));  // open: cin, cout
  Subtractor #(.width(16)) subtractor_1 (.a(operando_1_sub), .b(operando_2_sub), .out(subtracao));  // open: bin, bout
  assign \and  = operando_1_and & operando_2_and;  // AND_Gate and_1, 16 bits wide
  assign \or  = operando_1_or | operando_2_or;  // OR_Gate or_1, 16 bits wide
  assign \nand  = ~(operando_1_nand & operando_2_nand);  // NAND_Gate nand_1, 16 bits wide
  BitSelector #(.width(16), .group(4)) bitselector_1 (.in(operando_2_sll), .out(bitselector_1_out), .sel(2'b00));
  BitSelector #(.width(16), .group(4)) bitselector_2 (.in(operando_2_srl), .out(bitselector_2_out), .sel(2'b00));
  assign \nor  = ~(operando_1_nor | operando_2_nor);  // NOR_Gate nor_1, 16 bits wide
  Shifter #(.width(16)) shifter_1 (.in(operando_1_sll), .\dist (bitselector_1_out), .out(shift_left));
  Shifter #(.width(16), .shift("lr")) shifter_2 (.in(operando_1_srl), .\dist (bitselector_2_out), .out(shift_right));
  Comparator #(.width(16)) comparator_1 (.a(operando_1beq), .b(operando_2_beq), .eq(resultado_beq));  // open: gt, lt
  Comparator #(.width(16)) comparator_2 (.a(operando_1_bne), .b(operando_2_bne), .eq(comparator_2_eq));  // open: gt, lt
  not not_1 (resultado_bne, comparator_2_eq);
  Comparator #(.width(4)) comparator_3 (.a(4'b1000), .b(Funct), .eq(comparator_3_eq));  // open: gt, lt
  Comparator #(.width(4)) comparator_4 (.a(4'b1001), .b(Funct), .eq(comparator_4_eq));  // open: gt, lt
  Multiplexer #(.select(4), .width(16)) multiplexer_1 (
    .in0(soma), .in1(subtracao), .in2(\and ), .in3(\or ), .in4(\nand ), .in5(\nor ), .in6(shift_left),
    .in7(shift_right), .out(\Saída ), .sel(Funct));  // open: in8, in9, in10, in11, in12, in13, in14, in15, en
  and and_2 (and_2_out, comparator_3_eq, 1'b1);
  and and_3 (and_3_out, and_2_out, resultado_beq);
  and and_4 (and_4_out, resultado_bne, and_5_out);
  and and_5 (and_5_out, 1'b1, comparator_4_eq);
  or or_2 (Zero, and_3_out, and_4_out);
endmodule

module Unidade_de_Controle (
  input  [2:0] Opcode,
  output [3:0] out_2,
  output REG_WRITE,
  output BRANCH,
  output IMMEDIATE,
  output JUMP,
  output STORE,
  output LOAD,
  output FUNCT
);

  wire decoder_1_out1, decoder_1_out2, decoder_1_out3, decoder_1_out4, or_1_out;

  Decoder #(.select(3)) decoder_1 (
    .out0(FUNCT), .out1(decoder_1_out1), .out2(decoder_1_out2), .out3(decoder_1_out3), .out4(decoder_1_out4),
    .out5(LOAD), .out6(STORE), .out7(JUMP), .sel(Opcode));  // open: en
  Multiplexer #(.width(4)) multiplexer_1 (.in1(4'b0000), .out(out_2), .sel(or_1_out));  // open: in0, en
  or or_1 (or_1_out, decoder_1_out1, LOAD, STORE);
  or or_2 (IMMEDIATE, LOAD, decoder_1_out1, STORE, decoder_1_out2);
  Multiplexer #(.width(4)) multiplexer_2 (.in1(4'b0010), .out(out_2), .sel(decoder_1_out2));  // open: in0, en
  or or_3 (BRANCH, decoder_1_out3, decoder_1_out4);
  or or_4 (REG_WRITE, FUNCT, decoder_1_out1, decoder_1_out2, LOAD);
  Multiplexer #(.width(4)) multiplexer_3 (.in1(4'b1000), .out(out_2), .sel(decoder_1_out3));  // open: in0, en
  Multiplexer #(.width(4)) multiplexer_4 (.in1(4'b1001), .out(out_2), .sel(decoder_1_out4));  // open: in0, en

  // Other names for the same wires on the sheet: OPERATION[3:0] = out_2

  // Notes on the sheet:
  //   ADDI
  //   ANDI
  //   BEQ
  //   BNE
endmodule

// Diferenciar Reg. Escrita
module Diff__Reg__Escrita (
  input  [2:0] J_Registrador,
  input  [2:0] Opcode,
  output [2:0] Reg__Escrita
);

  wire multiplexer_1_out;

  Multiplexer #(.select(4)) multiplexer_1 (
    .in0(1'b0), .in1(1'b0), .in2(1'b0), .in3(1'b0), .in4(1'b0), .in5(1'b0), .in6(1'b0), .in7(1'b0),
    .in8(1'b0), .in9(1'b1), .out(multiplexer_1_out), .sel({1'b0, Opcode}));  // open: in10, in11, in12, in13, in14, in15, en
  Multiplexer #(.width(3)) multiplexer_2 (
    .in0(3'b111), .in1(J_Registrador), .out(Reg__Escrita), .sel(multiplexer_1_out));  // open: en

  // Other names for the same wires on the sheet: Opcode_t[2:0] = Opcode

  // Notes on the sheet:
  //   Acumulador
  //   Reg. mv
endmodule

module Diff__Fonte_Escrita_de_Dados (
  input  [15:0] \Saída_ULA ,
  input  [15:0] \Saída_Mem__Dados ,
  input  Load,
  input  Sinal_mv,
  input  [15:0] Acumulador,
  output [15:0] Escrita_de_Dados
);

  wire [15:0] multiplexer_1_out;

  Multiplexer #(.width(16)) multiplexer_1 (
    .in0(\Saída_ULA ), .in1(\Saída_Mem__Dados ), .out(multiplexer_1_out), .sel(Load));  // open: en
  Multiplexer #(.width(16)) multiplexer_2 (
    .in0(multiplexer_1_out), .in1(Acumulador), .out(Escrita_de_Dados), .sel(Sinal_mv));  // open: en
endmodule

module Extrator_Bits_Registradores (
  input  [3:0] \Reg__Fonte_1_Pré ,
  input  Imediato,
  input  Branch,
  input  [12:0] \J_Endereço ,
  output [3:0] \Reg__Fonte_1_Pós ,
  output [2:0] \J_Endereço_ou_Registrador_Pós 
);

  wire or_1_out;

  Multiplexer #(.width(4)) multiplexer_1 (
    .in0(\Reg__Fonte_1_Pré ), .in1(\Reg__Fonte_1_Pré ), .out(\Reg__Fonte_1_Pós ), .sel(or_1_out));  // open: en
  or or_1 (or_1_out, Imediato, Branch);

  assign \J_Endereço_ou_Registrador_Pós  = \J_Endereço [2:0];

  // Other names for the same wires on the sheet: Reg__Fonte_1_Pós_t[3:0] = \Reg__Fonte_1_Pré ;
  //   Tipo_I_Reg__Fonte_1_Pós[3:0] = \Reg__Fonte_1_Pré 
endmodule

module Concatenar_Jump (
  input  [12:0] Jump,
  input  [15:0] PC_atual,
  output [15:0] \Endereço_Final 
);


  assign \Endereço_Final  = {PC_atual[15:13], Jump};
endmodule

module \Verif__Se_É_Desvio_no_Tipo_I  (
  input  [2:0] Opcode,
  output \Saída 
);

  wire comparator_1_eq, comparator_2_eq, comparator_3_eq, comparator_4_eq;

  Comparator #(.width(4)) comparator_1 (.a(4'b0100), .b({1'b0, Opcode}), .eq(comparator_1_eq));  // open: gt, lt
  Comparator #(.width(4)) comparator_2 (.a(4'b1001), .b({1'b0, Opcode}), .eq(comparator_2_eq));  // open: gt, lt
  Comparator #(.width(4)) comparator_3 (.a(4'b0101), .b({1'b0, Opcode}), .eq(comparator_3_eq));  // open: gt, lt
  Comparator #(.width(4)) comparator_4 (.a(4'b0111), .b({1'b0, Opcode}), .eq(comparator_4_eq));  // open: gt, lt
  or or_1 (\Saída , comparator_1_eq, comparator_2_eq, comparator_3_eq, comparator_4_eq);

  // Other names for the same wires on the sheet: Opcode_t[2:0] = Opcode
endmodule

module Calcular_Desvio (
  input  [15:0] \Próx__End ,
  input  [15:0] \I_Constante_ou_Endereço ,
  output [15:0] End__Branch
);

  Adder #(.width(16)) adder_1 (.a(\Próx__End ), .b(\I_Constante_ou_Endereço ), .out(End__Branch));  // open: cin, cout
endmodule

module \Verif__Se_é_Desvio_Do_Tipo_I_ou_mv___ULA  (
  input  [2:0] Opcode,
  output \Saída 
);

  wire comparator_1_eq, comparator_2_eq;

  Comparator #(.width(4)) comparator_1 (.a(4'b0100), .b({1'b0, Opcode}), .eq(comparator_1_eq));  // open: gt, lt
  Comparator #(.width(4)) comparator_2 (.a(4'b0101), .b({1'b0, Opcode}), .eq(comparator_2_eq));  // open: gt, lt
  or or_1 (\Saída , comparator_1_eq, comparator_2_eq);

  // Other names for the same wires on the sheet: Opcode_t[2:0] = Opcode
endmodule

// Clock Inicial
module Gerenciador_Clock_Inicial (
  input  Clock,
  input  [15:0] PC_Atual,
  output Clock_Inicial
);

  wire comparator_1_eq, not_1_out;
  wire [15:0] \input_end_inicio_programa_1_end__início_do_programa ;

  Input_End__Inicio_Programa input_end_inicio_programa_1 (.\End__Início_do_Programa (\input_end_inicio_programa_1_end__início_do_programa ));
  Multiplexer multiplexer_1 (.in0(Clock), .in1(not_1_out), .out(Clock_Inicial), .sel(comparator_1_eq));  // open: en
  not not_1 (not_1_out, Clock);
  Comparator #(.width(16)) comparator_1 (
    .a(PC_Atual), .b(\input_end_inicio_programa_1_end__início_do_programa ), .eq(comparator_1_eq));  // open: gt, lt
endmodule

module Selecionar_Funct_ou_Operation (
  input  [3:0] Operation_ALU,
  input  [2:0] Opcode,
  input  Sinal_Funct,
  output [3:0] out_4
);

  Multiplexer #(.width(4)) multiplexer_1 (
    .in0(Operation_ALU), .in1({1'b0, Opcode}), .out(out_4), .sel(Sinal_Funct));  // open: en
endmodule

module PC (
  input  [15:0] \Endereço ,
  input  Reset,
  input  Branch,
  input  Pre_store,
  input  Load,
  input  Cache_Miss,
  input  Ciclo_Posterior_ao_Store,
  input  Fim_do_Load,
  input  Clock,
  input  Cache_Miss_Load,
  input  Ocorreu_Cache_Miss_Load,
  input  Ocorreu_Cache_Miss,
  output [15:0] PC_Atual
);

  wire and_1_out, and_2_out, and_3_out, comparator_1_eq, \delayer_1_saída , \delayer_2_saída , or_1_out;
  wire [15:0] \input_end_inicio_programa_1_end__início_do_programa , multiplexer_1_out, PC_Atual_t;

  Multiplexer #(.width(16)) multiplexer_1 (
    .in0(\Endereço ), .in1(PC_Atual_t), .out(multiplexer_1_out), .sel(\delayer_1_saída ));  // open: en
  Delayer delayer_1 (.\Saída (\delayer_1_saída ), .Entrada(and_1_out));
  and and_1 (and_1_out, ~Fim_do_Load, or_1_out);  // AND_Gate
  or or_1 (or_1_out, and_3_out, and_2_out, Ocorreu_Cache_Miss, Ocorreu_Cache_Miss_Load, Cache_Miss_Load);
  Delayer delayer_2 (.\Saída (\delayer_2_saída ), .Entrada(Clock));
  and and_2 (and_2_out, ~Ciclo_Posterior_ao_Store, Pre_store);  // AND_Gate
  and and_3 (and_3_out, ~Fim_do_Load, Cache_Miss);  // AND_Gate
  Registrador PC (
    .Entrada(multiplexer_1_out), .Clock(\delayer_2_saída ), .RESET(Reset), .\Saída (PC_Atual_t));  // open: Enable
  Input_End__Inicio_Programa input_end_inicio_programa_1 (.\End__Início_do_Programa (\input_end_inicio_programa_1_end__início_do_programa ));
  Comparator #(.width(16)) comparator_1 (.a(PC_Atual_t), .b({16{1'b0}}), .eq(comparator_1_eq));  // open: gt, lt
  Multiplexer #(.width(16)) multiplexer_2 (
    .in0(PC_Atual_t), .in1(\input_end_inicio_programa_1_end__início_do_programa ), .out(PC_Atual),
    .sel(comparator_1_eq));  // open: en

  // Other names for the same wires on the sheet: Pré_store = Pre_store
endmodule

module Memoria_Principal (
  input  [15:0] End__L_S_ULA,
  input  [15:0] End__Leitura_PC,
  input  Pre_store,
  input  Clock,
  input  Store,
  input  Reset,
  input  Load,
  input  Cache_Miss,
  input  Cache_Miss_Load,
  input  Primeiro_Ciclo,
  input  Fim_do_Programa,
  input  [15:0] Entrada_Dado_a_ser_Escrito,
  output Escrever_na_Cache,
  output [15:0] \Saída_1 ,
  output [15:0] \Saída_2 ,
  output [15:0] \Saída_3 ,
  output [15:0] \Saída_4 ,
  output Escrever_Bloco_Load
);

  wire and_1_out, Clock_t, comparator_1_eq, Escrever_Dados, Escrever_Sub_Mem__0, Escrever_Sub_Mem__1,
       Escrever_Sub_Mem__2, Escrever_Sub_Mem__3, Escrita_Sub_Mem__1, Escrita_Sub_Mem__2, Escrita_Sub_Mem__3,
       Escrita_Sub_Mem__4, \Habilitar_Memória_0 , \Habilitar_Memória_1 , \Habilitar_Memória_2 ,
       \Habilitar_Memória_3 , not_1_out, not_2_out, not_3_out, not_4_out, \É_início_do_Programa ;
  wire [1:0] Sub_Mem__Escrita;
  wire [9:0] End__L_S_ULA_t, End__PC, \Nº_do_Bloco , \Sub_Memória ;
  wire [15:0] Entrada_1, Entrada_2, Entrada_3, Entrada_4,
       \input_end_inicio_programa_1_end__início_do_programa ;

  BitSelector #(.width(16), .group(10)) bitselector_1 (.in(End__L_S_ULA), .out(End__L_S_ULA_t), .sel(1'b0));
  BitSelector #(.width(16), .group(10)) bitselector_2 (.in(End__Leitura_PC), .out(End__PC), .sel(1'b0));
  Gerenciador_Clock_Inicial gerenciador_clock_inicial_1 (
    .Clock_Inicial(Clock_t), .Clock(Clock), .PC_Atual(End__Leitura_PC));
  RAM #(.addrWidth(10), .dataWidth(16), .bus("asynch")) ram_1 (
    .addr(\Nº_do_Bloco ), .data(\Saída_1 ), .sel(\Habilitar_Memória_0 ), .ld(not_1_out), .clr(Reset));
  not not_1 (not_1_out, Escrever_Sub_Mem__0);
  RAM #(.addrWidth(10), .dataWidth(16), .bus("asynch")) ram_2 (
    .addr(\Nº_do_Bloco ), .data(\Saída_2 ), .sel(\Habilitar_Memória_1 ), .ld(not_2_out), .clr(Reset));
  not not_2 (not_2_out, Escrever_Sub_Mem__1);
  assign \Saída_1  = Escrever_Sub_Mem__0 ? Entrada_1 : 16'bz;  // Controlled_Buffer controlled_buffer_1
  assign \Saída_2  = Escrever_Sub_Mem__1 ? Entrada_2 : 16'bz;  // Controlled_Buffer controlled_buffer_2
  \Calcular_Endereço  \calcular_endereço_1  (
    .End__L_S_ULA(End__L_S_ULA_t), .End__PC(End__PC), .Cache_Miss_Load(Cache_Miss_Load),
    .Escrever_Dados(Escrever_Dados), .Primeiro_Ciclo(Primeiro_Ciclo), .Store(Store), .Load(Load),
    .Numero_do_Bloco(\Nº_do_Bloco ), .\Sub_Memória (\Sub_Memória ), .Pre_store(Pre_store));
  Direcionar_Dados_Entrada_MP direcionar_dados_entrada_mp_1 (
    .Escrever_Dados(Escrever_Dados), .\Sub_Memória (\Sub_Memória ),
    .Entrada_Dado_a_ser_Escrito(Entrada_Dado_a_ser_Escrito), .Entrada_1(Entrada_1), .Entrada_2(Entrada_2),
    .Entrada_3(Entrada_3), .Entrada_4(Entrada_4), .Escrita_Sub_Mem__1(Escrita_Sub_Mem__1),
    .Escrita_Sub_Mem__2(Escrita_Sub_Mem__2), .Escrita_Sub_Mem__3(Escrita_Sub_Mem__3),
    .Escrita_Sub_Mem__4(Escrita_Sub_Mem__4), .Sub_Mem__Escrita(Sub_Mem__Escrita), .Store(Store));
  RAM #(.addrWidth(10), .dataWidth(16), .bus("asynch")) ram_3 (
    .addr(\Nº_do_Bloco ), .data(\Saída_3 ), .sel(\Habilitar_Memória_2 ), .ld(not_3_out), .clr(Reset));
  assign \Saída_3  = Escrever_Sub_Mem__2 ? Entrada_3 : 16'bz;  // Controlled_Buffer controlled_buffer_3
  not not_3 (not_3_out, Escrever_Sub_Mem__2);
  RAM #(.addrWidth(10), .dataWidth(16), .bus("asynch")) ram_4 (
    .addr(\Nº_do_Bloco ), .data(\Saída_4 ), .sel(\Habilitar_Memória_3 ), .ld(not_4_out), .clr(Reset));
  assign \Saída_4  = Escrever_Sub_Mem__3 ? Entrada_4 : 16'bz;  // Controlled_Buffer controlled_buffer_4
  not not_4 (not_4_out, Escrever_Sub_Mem__3);
  Buffer_Sinais_Escrita buffer_sinais_escrita_1 (
    .Clock(Clock_t), .Escrita_Sub_Mem__1(Escrita_Sub_Mem__1), .Clock_Fonte(Clock),
    .Fim_do_Programa(Fim_do_Programa), .Store(Store), .\Escrever_Na_Memória_0 (Escrever_Sub_Mem__0),
    .Escrita_Sub_Mem__2(Escrita_Sub_Mem__2), .Escrita_Sub_Mem__3(Escrita_Sub_Mem__3),
    .Escrita_Sub_Mem__4(Escrita_Sub_Mem__4), .\Escrever_Na_Memória_1 (Escrever_Sub_Mem__1),
    .\Escrever_Na_Memória_2 (Escrever_Sub_Mem__2), .\Escrever_Na_Memória_3 (Escrever_Sub_Mem__3),
    .\É_Início_do_Programa (\É_início_do_Programa ), .End__L_S_ULA(End__L_S_ULA_t),
    .Sub_Mem__Escrita(Sub_Mem__Escrita));
  \Habilitar_Memória  \u_habilitar_memória_1  (
    .Clock(Clock_t), .Escrita_Sub_Mem__1(Escrita_Sub_Mem__1), .Clock_Fonte(Clock), .Store(Store),
    .\Habilitar_Memória_1 (\Habilitar_Memória_0 ), .\Habilitar_Memória_2 (\Habilitar_Memória_1 ),
    .\Habilitar_Memória_3 (\Habilitar_Memória_2 ), .\Habilitar_Memória_4 (\Habilitar_Memória_3 ),
    .Escrita_Sub_Mem__2(Escrita_Sub_Mem__2), .Escrita_Sub_Mem__3(Escrita_Sub_Mem__3),
    .Escrita_Sub_Mem__4(Escrita_Sub_Mem__4), .\É_início_do_Programa (\É_início_do_Programa ));
  Input_End__Inicio_Programa input_end_inicio_programa_1 (.\End__Início_do_Programa (\input_end_inicio_programa_1_end__início_do_programa ));
  and and_1 (and_1_out, Clock_t, ~Escrever_Bloco_Load, Primeiro_Ciclo);  // AND_Gate
  and and_2 (Escrever_Bloco_Load, Load, Cache_Miss_Load);
  Comparator #(.width(16)) comparator_1 (
    .a(\input_end_inicio_programa_1_end__início_do_programa ), .b(End__Leitura_PC), .eq(comparator_1_eq));  // open: gt, lt
  or or_1 (Escrever_na_Cache, and_1_out, Store, Cache_Miss);
  and and_3 (\É_início_do_Programa , comparator_1_eq, Clock_t);
  and and_4 (Escrever_Dados, Store, ~Clock);  // AND_Gate

  // Other names for the same wires on the sheet: Clock_Fonte = Clock; Pré_End__PC[15:0] = End__Leitura_PC

  // Notes on the sheet:
  //   Sub. Memória 0
  //   Sub. Memória 1
  //   Sub. Memória 2
  //   Sub. Memória 3
endmodule

module Input_End__Inicio_Programa (
  output [15:0] \End__Início_do_Programa 
);


  assign \End__Início_do_Programa  = 16'h6c;
endmodule

module Linha_da_Cache_Direta (
  input  [15:0] Palavra_1,
  input  [15:0] Palavra_2,
  input  [15:0] Palavra_3,
  input  [15:0] Palavra_4,
  input  Reset,
  input  [1:0] Palavra_L_S,
  input  Escrita,
  input  [1:0] Palavra,
  input  Clock,
  output [15:0] \Saída_Instrução_PC ,
  output [15:0] \Saída_L_S 
);

  wire and_1_out;
  wire [15:0] \registrador_1_saída , \registrador_2_saída , \registrador_3_saída , \registrador_4_saída ;

  and and_1 (and_1_out, Escrita, ~Clock);  // AND_Gate
  Registrador registrador_1 (
    .Entrada(Palavra_1), .Clock(and_1_out), .RESET(Reset), .\Saída (\registrador_1_saída ));  // open: Enable
  Registrador registrador_2 (
    .Entrada(Palavra_2), .Clock(and_1_out), .RESET(Reset), .\Saída (\registrador_2_saída ));  // open: Enable
  Registrador registrador_3 (
    .Entrada(Palavra_3), .Clock(and_1_out), .RESET(Reset), .\Saída (\registrador_3_saída ));  // open: Enable
  Registrador registrador_4 (
    .Entrada(Palavra_4), .Clock(and_1_out), .RESET(Reset), .\Saída (\registrador_4_saída ));  // open: Enable
  Multiplexer #(.select(2), .width(16)) multiplexer_1 (
    .in0(\registrador_1_saída ), .in1(\registrador_2_saída ), .in2(\registrador_3_saída ),
    .in3(\registrador_4_saída ), .out(\Saída_Instrução_PC ), .sel(Palavra));  // open: en
  Multiplexer #(.select(2), .width(16)) multiplexer_2 (
    .in0(\registrador_1_saída ), .in1(\registrador_2_saída ), .in2(\registrador_3_saída ),
    .in3(\registrador_4_saída ), .out(\Saída_L_S ), .sel(Palavra_L_S));  // open: en
endmodule

module Cache_Direta (
  input  [15:0] Entrada_1,
  input  [15:0] Entrada_2,
  input  [15:0] Entrada_3,
  input  [15:0] Entrada_4,
  input  [15:0] \Endereço_PC ,
  input  [15:0] \Endereço_L_S ,
  input  [15:0] \Saída_2_Banco ,
  input  Escrita,
  input  Reset,
  input  Primeiro_Ciclo,
  input  Load,
  input  Store,
  input  Ciclo_Posterior_ao_Store,
  input  Pre_store,
  input  Clock,
  input  Escrever_Bloco_Load,
  output [15:0] \Saída ,
  output [15:0] \Saída_Load ,
  output [15:0] End__Cache_Miss,
  output Cache_Miss,
  output Cache_Miss_Load
);

  wire and_1_out, and_2_out, and_3_out, and_4_out, and_5_out, and_6_out, and_7_out, and_8_out, and_9_out,
       and_10_out, and_11_out, and_12_out, and_13_out, and_14_out, and_15_out, and_16_out, and_17_out,
       and_18_out, and_19_out, Bloco_Com_a_Instrucao_esta_na_cache, Bloco_Com_o_dado_do_Load_esta_na_cache,
       Cache_Miss_t, Clock_t, \Clock_Válido_e_TAG , \Enable_Válido_e_TAG , Escrita_Linha_0, Escrita_Linha_1,
       Escrita_Linha_2, Escrita_Linha_3, Escrita_Linha_4, Escrita_Linha_5, Escrita_Linha_6, Escrita_Linha_7,
       \Início_Prog , multiplexer_3_out, nand_2_out, not_1_out, or_1_out, or_2_out, \Válido_Linha_0 ,
       \Válido_Linha_1 , \Válido_Linha_2 , \Válido_Linha_3 , \Válido_Linha_4 , \Válido_Linha_5 ,
       \Válido_Linha_6 , \Válido_Linha_7 , \Válido_Linha_com_dado_Load , \Válido_Linha_Instrucao ;
  wire [1:0] Palavra, Palavra_L_S;
  wire [2:0] Linha, Linha__L_S;
  wire [4:0] multiplexer_1_out, multiplexer_2_out, TAG, TAG__L_S, TAG_Linha_0, TAG_Linha_1, TAG_Linha_2,
       TAG_Linha_3, TAG_Linha_4, TAG_Linha_5, TAG_Linha_6, TAG_Linha_7;
  wire [15:0] Entrada_1_t, Entrada_2_t, Entrada_3_t, Entrada_4_t, \Saída_0_Instrução , \Saída_0_L_S ,
       \Saída_1_Instrução , \Saída_1_L_S , \Saída_2__L_S , \Saída_2_Instrução , \Saída_3__L_S ,
       \Saída_3_Instrução , \Saída_4_Instrução , \Saída_4_L_S , \Saída_5__L_S , \Saída_5_Instrução ,
       \Saída_6_Instrução , \Saída_6_L_S , \Saída_7_Instrução , \Saída_7_L_S ;

  BitSelector #(.width(16), .group(10)) bitselector_1 (.in(\Endereço_PC ), .out({TAG, Linha, Palavra}), .sel(1'b0));
  BitSelector #(.width(16), .group(10)) bitselector_2 (
    .in(\Endereço_L_S ), .out({TAG__L_S, Linha__L_S, Palavra_L_S}), .sel(1'b0));
  Buffer_Store buffer_store_1 (
    .Clock(Clock_t), .Ciclo_Posterior_ao_Store(Ciclo_Posterior_ao_Store), .Pre_store(Pre_store),
    .Entrada_Mem__1(Entrada_1), .Entrada_Mem__3(Entrada_3), .Palavra_L_S(Palavra_L_S),
    .Dado_Store(\Saída_2_Banco ), .Entrada_Mem__2(Entrada_2), .Entrada_Mem__4(Entrada_4),
    .Entrada_1(Entrada_1_t), .Entrada_3(Entrada_3_t), .Entrada_2(Entrada_2_t), .Entrada_4(Entrada_4_t));
  \Início_do_Programa_Handler  \início_do_programa_handler_1  (
    .\Endereço_from_PC (\Endereço_PC ), .Clock_Fonte(Clock), .\Enable_Válido_e_TAG (\Enable_Válido_e_TAG ),
    .\Clock_Válido_e_TAG (\Clock_Válido_e_TAG ), .Clock(Clock_t), .\Início_Prog (\Início_Prog ),
    .Escrever_Bloco_Load(Escrever_Bloco_Load));
  Linha_de_Escrita_Handler linha_de_escrita_handler_1 (
    .Escrita_Linha_0(Escrita_Linha_0), .Escrita_Linha_4(Escrita_Linha_4), .Escrita_Linha_1(Escrita_Linha_1),
    .Escrita_Linha_5(Escrita_Linha_5), .Escrita_Linha_2(Escrita_Linha_2), .Escrita_Linha_6(Escrita_Linha_6),
    .Escrita_Linha_3(Escrita_Linha_3), .Escrita_Linha_7(Escrita_Linha_7),
    .Escrever_Bloco_Load(Escrever_Bloco_Load), .Load(Load), .Linha__L_S(Linha__L_S), .Clock(Clock_t),
    .\Início_Prog (Primeiro_Ciclo), .Escrita(Escrita), .Linha(Linha),
    .Ciclo_Posterior_ao_Store(Ciclo_Posterior_ao_Store));
  and and_1 (and_1_out, Escrita_Linha_0, ~\Enable_Válido_e_TAG );  // AND_Gate
  and and_2 (and_2_out, Escrita_Linha_1, ~\Enable_Válido_e_TAG );  // AND_Gate
  and and_3 (and_3_out, Escrita_Linha_2, ~\Enable_Válido_e_TAG );  // AND_Gate
  and and_4 (and_4_out, Escrita_Linha_3, ~\Enable_Válido_e_TAG );  // AND_Gate
  and and_5 (and_5_out, Escrita_Linha_4, ~\Enable_Válido_e_TAG );  // AND_Gate
  and and_6 (and_6_out, Escrita_Linha_5, ~\Enable_Válido_e_TAG );  // AND_Gate
  and and_7 (and_7_out, Escrita_Linha_6, ~\Enable_Válido_e_TAG );  // AND_Gate
  and and_8 (and_8_out, Escrita_Linha_7, ~\Enable_Válido_e_TAG );  // AND_Gate
  \Verificar_se_O_Bloco_Está_na_Cache  \verificar_se_o_bloco_está_na_cache_1  (
    .TAG_Linha_0(TAG_Linha_0), .TAG_Linha_1(TAG_Linha_1), .TAG_Linha_2(TAG_Linha_2),
    .TAG_Linha_3(TAG_Linha_3), .TAG_Linha_4(TAG_Linha_4), .TAG_Linha_5(TAG_Linha_5),
    .TAG_Linha_6(TAG_Linha_6), .TAG_Linha_7(TAG_Linha_7),
    .Bloco_Com_a_Instrucao_esta_na_cache(Bloco_Com_a_Instrucao_esta_na_cache),
    .Bloco_Com_o_dado_do_Load_esta_na_cache(Bloco_Com_o_dado_do_Load_esta_na_cache), .TAG(TAG),
    .Linha(Linha), .TAG__L_S(TAG__L_S), .Linha__L_S(Linha__L_S), .Load(Load));
  Register #(.width(1)) register_1 (
    .D(1'b1), .en(and_1_out), .Q(\Válido_Linha_0 ), .clk(\Clock_Válido_e_TAG ));  // open: clr
  Register #(.width(1)) register_2 (
    .D(1'b1), .en(and_2_out), .Q(\Válido_Linha_1 ), .clk(\Clock_Válido_e_TAG ));  // open: clr
  Register #(.width(1)) register_3 (
    .D(1'b1), .en(and_3_out), .Q(\Válido_Linha_2 ), .clk(\Clock_Válido_e_TAG ));  // open: clr
  Register #(.width(1)) register_4 (
    .D(1'b1), .en(and_4_out), .Q(\Válido_Linha_3 ), .clk(\Clock_Válido_e_TAG ));  // open: clr
  Register #(.width(1)) register_5 (
    .D(1'b1), .en(and_5_out), .Q(\Válido_Linha_4 ), .clk(\Clock_Válido_e_TAG ));  // open: clr
  Register #(.width(1)) register_6 (
    .D(1'b1), .en(and_6_out), .Q(\Válido_Linha_5 ), .clk(\Clock_Válido_e_TAG ));  // open: clr
  Register #(.width(1)) register_7 (
    .D(1'b1), .en(and_7_out), .Q(\Válido_Linha_6 ), .clk(\Clock_Válido_e_TAG ));  // open: clr
  Register #(.width(1)) register_8 (
    .D(1'b1), .en(and_8_out), .Q(\Válido_Linha_7 ), .clk(\Clock_Válido_e_TAG ));  // open: clr
  or or_1 (or_1_out, Ciclo_Posterior_ao_Store, Escrever_Bloco_Load);
  Multiplexer #(.width(5)) multiplexer_1 (
    .in0(TAG), .in1(TAG__L_S), .out(multiplexer_1_out), .sel(or_1_out));  // open: en
  Register #(.width(5)) register_9 (
    .D(multiplexer_1_out), .en(and_9_out), .Q(TAG_Linha_0), .clk(\Clock_Válido_e_TAG ));  // open: clr
  and and_9 (and_9_out, Escrita_Linha_0, ~\Enable_Válido_e_TAG );  // AND_Gate
  Register #(.width(5)) register_10 (
    .D(multiplexer_1_out), .en(and_10_out), .Q(TAG_Linha_1), .clk(\Clock_Válido_e_TAG ));  // open: clr
  and and_10 (and_10_out, Escrita_Linha_1, ~\Enable_Válido_e_TAG );  // AND_Gate
  Register #(.width(5)) register_11 (
    .D(multiplexer_1_out), .en(and_11_out), .Q(TAG_Linha_2), .clk(\Clock_Válido_e_TAG ));  // open: clr
  and and_11 (and_11_out, Escrita_Linha_2, ~\Enable_Válido_e_TAG );  // AND_Gate
  Register #(.width(5)) register_12 (
    .D(multiplexer_1_out), .en(and_12_out), .Q(TAG_Linha_3), .clk(\Clock_Válido_e_TAG ));  // open: clr
  and and_12 (and_12_out, Escrita_Linha_3, ~\Enable_Válido_e_TAG );  // AND_Gate
  or or_2 (or_2_out, Ciclo_Posterior_ao_Store, Escrever_Bloco_Load);
  Multiplexer #(.width(5)) multiplexer_2 (
    .in0(TAG), .in1(TAG__L_S), .out(multiplexer_2_out), .sel(or_2_out));  // open: en
  and and_13 (and_13_out, Escrita_Linha_4, ~\Enable_Válido_e_TAG );  // AND_Gate
  and and_14 (and_14_out, Escrita_Linha_5, ~\Enable_Válido_e_TAG );  // AND_Gate
  and and_15 (and_15_out, Escrita_Linha_6, ~\Enable_Válido_e_TAG );  // AND_Gate
  and and_16 (and_16_out, Escrita_Linha_7, ~\Enable_Válido_e_TAG );  // AND_Gate
  Register #(.width(5)) register_13 (
    .D(multiplexer_2_out), .en(and_13_out), .Q(TAG_Linha_4), .clk(\Clock_Válido_e_TAG ));  // open: clr
  Register #(.width(5)) register_14 (
    .D(multiplexer_2_out), .en(and_14_out), .Q(TAG_Linha_5), .clk(\Clock_Válido_e_TAG ));  // open: clr
  Register #(.width(5)) register_15 (
    .D(multiplexer_2_out), .en(and_15_out), .Q(TAG_Linha_6), .clk(\Clock_Válido_e_TAG ));  // open: clr
  Register #(.width(5)) register_16 (
    .D(multiplexer_2_out), .en(and_16_out), .Q(TAG_Linha_7), .clk(\Clock_Válido_e_TAG ));  // open: clr
  \Verificar_se_a_Linha_é_Válida  \verificar_se_a_linha_é_válida_1  (
    .\Válido_Linha_0 (\Válido_Linha_0 ), .\Válido_Linha_1 (\Válido_Linha_1 ),
    .\Válido_Linha_2 (\Válido_Linha_2 ), .\Válido_Linha_3 (\Válido_Linha_3 ),
    .\Válido_Linha_4 (\Válido_Linha_4 ), .\Válido_Linha_5 (\Válido_Linha_5 ),
    .\Válido_Linha_6 (\Válido_Linha_6 ), .\Válido_Linha_7 (\Válido_Linha_7 ),
    .\Válido_Linha_Instrucao (\Válido_Linha_Instrucao ),
    .\Válido_Linha_com_dado_Load (\Válido_Linha_com_dado_Load ), .Linha(Linha), .Linha__L_S(Linha__L_S));
  Multiplexer multiplexer_3 (
    .in0(1'b0), .in1(Bloco_Com_o_dado_do_Load_esta_na_cache), .out(multiplexer_3_out), .sel(Load));  // open: en
  Linha_da_Cache_Direta linha_da_cache_direta_1 (
    .Palavra_1(Entrada_1_t), .Palavra_2(Entrada_2_t), .Palavra_3(Entrada_3_t), .Palavra_4(Entrada_4_t),
    .Palavra(Palavra), .Clock(Clock_t), .Escrita(Escrita_Linha_0),
    .\Saída_Instrução_PC (\Saída_0_Instrução ), .Reset(Reset), .\Saída_L_S (\Saída_0_L_S ),
    .Palavra_L_S(Palavra_L_S));
  Linha_da_Cache_Direta linha_da_cache_direta_2 (
    .Palavra_1(Entrada_1_t), .Palavra_2(Entrada_2_t), .Palavra_3(Entrada_3_t), .Palavra_4(Entrada_4_t),
    .Palavra(Palavra), .Clock(Clock_t), .Escrita(Escrita_Linha_1),
    .\Saída_Instrução_PC (\Saída_1_Instrução ), .Reset(Reset), .\Saída_L_S (\Saída_1_L_S ),
    .Palavra_L_S(Palavra_L_S));
  Linha_da_Cache_Direta linha_da_cache_direta_3 (
    .Palavra_1(Entrada_1_t), .Palavra_2(Entrada_2_t), .Palavra_3(Entrada_3_t), .Palavra_4(Entrada_4_t),
    .Palavra(Palavra), .Clock(Clock_t), .Escrita(Escrita_Linha_2),
    .\Saída_Instrução_PC (\Saída_2_Instrução ), .Reset(Reset), .\Saída_L_S (\Saída_2__L_S ),
    .Palavra_L_S(Palavra_L_S));
  Linha_da_Cache_Direta linha_da_cache_direta_4 (
    .Palavra_1(Entrada_1_t), .Palavra_2(Entrada_2_t), .Palavra_3(Entrada_3_t), .Palavra_4(Entrada_4_t),
    .Palavra(Palavra), .Clock(Clock_t), .Escrita(Escrita_Linha_3),
    .\Saída_Instrução_PC (\Saída_3_Instrução ), .Reset(Reset), .\Saída_L_S (\Saída_3__L_S ),
    .Palavra_L_S(Palavra_L_S));
  Linha_da_Cache_Direta linha_da_cache_direta_5 (
    .Palavra_1(Entrada_1_t), .Palavra_2(Entrada_2_t), .Palavra_3(Entrada_3_t), .Palavra_4(Entrada_4_t),
    .Palavra(Palavra), .Clock(Clock_t), .Escrita(Escrita_Linha_4),
    .\Saída_Instrução_PC (\Saída_4_Instrução ), .Reset(Reset), .\Saída_L_S (\Saída_4_L_S ),
    .Palavra_L_S(Palavra_L_S));
  Linha_da_Cache_Direta linha_da_cache_direta_6 (
    .Palavra_1(Entrada_1_t), .Palavra_2(Entrada_2_t), .Palavra_3(Entrada_3_t), .Palavra_4(Entrada_4_t),
    .Palavra(Palavra), .Clock(Clock_t), .Escrita(Escrita_Linha_5),
    .\Saída_Instrução_PC (\Saída_5_Instrução ), .Reset(Reset), .\Saída_L_S (\Saída_5__L_S ),
    .Palavra_L_S(Palavra_L_S));
  Linha_da_Cache_Direta linha_da_cache_direta_7 (
    .Palavra_1(Entrada_1_t), .Palavra_2(Entrada_2_t), .Palavra_3(Entrada_3_t), .Palavra_4(Entrada_4_t),
    .Palavra(Palavra), .Clock(Clock_t), .Escrita(Escrita_Linha_6),
    .\Saída_Instrução_PC (\Saída_6_Instrução ), .Reset(Reset), .\Saída_L_S (\Saída_6_L_S ),
    .Palavra_L_S(Palavra_L_S));
  Linha_da_Cache_Direta linha_da_cache_direta_8 (
    .Palavra_1(Entrada_1_t), .Palavra_2(Entrada_2_t), .Palavra_3(Entrada_3_t), .Palavra_4(Entrada_4_t),
    .Palavra(Palavra), .Clock(Clock_t), .Escrita(Escrita_Linha_7),
    .\Saída_Instrução_PC (\Saída_7_Instrução ), .Reset(Reset), .\Saída_L_S (\Saída_7_L_S ),
    .Palavra_L_S(Palavra_L_S));
  nand nand_1 (Cache_Miss_t, Bloco_Com_a_Instrucao_esta_na_cache, \Válido_Linha_Instrucao );
  not not_1 (not_1_out, and_17_out);
  and and_17 (and_17_out, ~Primeiro_Ciclo, multiplexer_3_out);  // AND_Gate
  Multiplexer multiplexer_4 (.in0(1'b0), .in1(nand_2_out), .out(Cache_Miss_Load), .sel(and_18_out));  // open: en
  nand nand_2 (nand_2_out, Bloco_Com_o_dado_do_Load_esta_na_cache, \Válido_Linha_com_dado_Load );
  and and_18 (and_18_out, ~Cache_Miss_t, Load);  // AND_Gate
  Multiplexer multiplexer_5 (.in0(Cache_Miss_t), .in1(not_1_out), .out(Cache_Miss), .sel(and_19_out));  // open: en
  and and_19 (and_19_out, ~Cache_Miss_Load, Load);  // AND_Gate
  Multiplexer #(.select(3), .width(16)) multiplexer_6 (
    .in0(\Saída_0_Instrução ), .in1(\Saída_1_Instrução ), .in2(\Saída_2_Instrução ),
    .in3(\Saída_3_Instrução ), .in4(\Saída_4_Instrução ), .in5(\Saída_5_Instrução ),
    .in6(\Saída_6_Instrução ), .in7(\Saída_7_Instrução ), .out(\Saída ), .sel(Linha));  // open: en
  Multiplexer #(.select(3), .width(16)) multiplexer_7 (
    .in0(\Saída_0_L_S ), .in1(\Saída_1_L_S ), .in2(\Saída_2__L_S ), .in3(\Saída_3__L_S ),
    .in4(\Saída_4_L_S ), .in5(\Saída_5__L_S ), .in6(\Saída_6_L_S ), .in7(\Saída_7_L_S ), .out(\Saída_Load ),
    .sel(Linha__L_S));  // open: en

  assign End__Cache_Miss = \Endereço_PC ;

  // Other names for the same wires on the sheet: Clock_Fonte = Clock; Dado_Store[15:0] = \Saída_2_Banco ;
  //   Endereço__L_S[15:0] = \Endereço_L_S ; Endereço_from_PC[15:0] = \Endereço_PC ; Entrada_Mem__1[15:0] = Entrada_1;
  //   Entrada_Mem__2[15:0] = Entrada_2; Entrada_Mem__3[15:0] = Entrada_3; Entrada_Mem__4[15:0] = Entrada_4
endmodule

module Circuito_Principal (
  input  Reset
);

  wire Cache_Miss, Cache_Miss_Load, Ciclo_Posterior_ao_Store, Clock, Clock_Fonte, Escrever_Bloco_Load,
       Escrever_na_Cache, Fim_do_Programa, Load, Pre_store, Primeiro_Ciclo, Store;
  wire [15:0] Dado_Load_from_Cache, End__from_Cache, End__L_S, \Saída_2_Banco , \Saída_Cache , \Saída_Mem_2 ,
       \Saída_Mem__1 , \Saída_Mem__3 , \Saída_Mem__4 , \Saída_PC_Atual ;

  LED u_Fim_do_Programa (.in(Fim_do_Programa));
  Processador processador_1 (
    .\Saída_PC_Atual (\Saída_PC_Atual ), .\Instrução (\Saída_Cache ), .\Saída_2_Banco (\Saída_2_Banco ),
    .Load(Load), .Store(Store), .\Saída_ULA_L_S (End__L_S), .Reset(Reset), .Cache_Miss(Cache_Miss),
    .Entrada_Dado_Load(Dado_Load_from_Cache), .Cache_Miss_Load(Cache_Miss_Load),
    .Primeiro_Ciclo(Primeiro_Ciclo), .Pre_store(Pre_store),
    .Ciclo_Posterior_ao_Store(Ciclo_Posterior_ao_Store), .Clock_Fonte(Clock_Fonte),
    .Fim_do_Programa(Fim_do_Programa), .Clock(Clock));
  Memoria_Principal memoria_principal_1 (
    .Clock(Clock), .Reset(Reset), .Store(Store), .Escrever_na_Cache(Escrever_na_Cache), .Load(Load),
    .\Saída_1 (\Saída_Mem__1 ), .\Saída_3 (\Saída_Mem__3 ), .\Saída_2 (\Saída_Mem_2 ),
    .\Saída_4 (\Saída_Mem__4 ), .Cache_Miss(Cache_Miss), .Escrever_Bloco_Load(Escrever_Bloco_Load),
    .Cache_Miss_Load(Cache_Miss_Load), .Primeiro_Ciclo(Primeiro_Ciclo), .Fim_do_Programa(Fim_do_Programa),
    .End__Leitura_PC(End__from_Cache), .End__L_S_ULA(End__L_S), .Entrada_Dado_a_ser_Escrito(\Saída_2_Banco ),
    .Pre_store(Pre_store));
  Clock u_Clock (.out(Clock_Fonte));
  Cache_Direta cache_direta_1 (
    .Entrada_1(\Saída_Mem__1 ), .Entrada_2(\Saída_Mem_2 ), .Entrada_3(\Saída_Mem__3 ),
    .Entrada_4(\Saída_Mem__4 ), .\Endereço_PC (\Saída_PC_Atual ), .Escrita(Escrever_na_Cache), .Clock(Clock),
    .Reset(Reset), .\Endereço_L_S (End__L_S), .Load(Load), .Store(Store), .\Saída (\Saída_Cache ),
    .\Saída_Load (Dado_Load_from_Cache), .Escrever_Bloco_Load(Escrever_Bloco_Load),
    .Primeiro_Ciclo(Primeiro_Ciclo), .Pre_store(Pre_store), .\Saída_2_Banco (\Saída_2_Banco ),
    .Ciclo_Posterior_ao_Store(Ciclo_Posterior_ao_Store), .End__Cache_Miss(End__from_Cache),
    .Cache_Miss(Cache_Miss), .Cache_Miss_Load(Cache_Miss_Load));
endmodule

module Gerenciador_Clock (
  input  Clock,
  input  Cache_Miss,
  input  [15:0] \Saída_PC_Atual ,
  input  [15:0] \Saída_Cache ,
  output Fim_do_Programa
);

  wire Cache_Miss_Tratado, Clock_t, comparator_1_eq, comparator_2_eq;
  wire [15:0] \input_end_inicio_programa_1_end__início_do_programa ;

  Multiplexer multiplexer_1 (.in0(Clock), .in1(1'b0), .out(Clock_t), .sel(Fim_do_Programa));  // open: en
  Multiplexer multiplexer_2 (
    .in0(Cache_Miss), .in1(1'b0), .out(Cache_Miss_Tratado), .sel(Fim_do_Programa));  // open: en
  Comparator #(.width(16)) comparator_1 (
    .a(\Saída_PC_Atual ), .b(\input_end_inicio_programa_1_end__início_do_programa ), .eq(comparator_1_eq));  // open: gt, lt
  Input_End__Inicio_Programa input_end_inicio_programa_1 (.\End__Início_do_Programa (\input_end_inicio_programa_1_end__início_do_programa ));
  Comparator #(.width(16)) comparator_2 (.a(\Saída_Cache ), .b({16{1'b0}}), .eq(comparator_2_eq));  // open: gt, lt
  and and_1 (Fim_do_Programa, comparator_2_eq, ~Cache_Miss_Tratado, ~comparator_1_eq);  // AND_Gate
endmodule

module Cache_Miss_Load_Handler (
  input  Cache_Miss,
  input  Clock,
  input  Cache_Miss_Load,
  input  Load,
  input  [15:0] PC_Atual,
  input  [15:0] \Entrada_Instrução ,
  input  Ciclo_Posterior_ao_Store,
  output Primeiro_Ciclo,
  output [15:0] \Instrução ,
  output Ocorreu_Cache_Miss_Dado_Load,
  output Fim_do_Load,
  output Ocorreu_Cache_Miss
);

  wire and_1_out, and_2_out, and_3_out, and_4_out, and_5_out, and_6_out, and_7_out, and_8_out, and_9_out,
       and_10_out, Cache_Miss___Segunda_Metade_do_Ciclo, Ciclo_Posterior_ao_Cache_Miss_Dado_Load,
       \delayer_1_saída , \delayer_2_saída , \delayer_3_saída , \delayer_4_saída , \delayer_5_saída ,
       \delayer_6_saída , Inicio_do_Programa, Ocorreu_Cache_Miss_t, or_1_out, register_1_q;
  wire [15:0] \input_end_inicio_programa_1_end__início_do_programa , \Instrução_Buffer ;

  Input_End__Inicio_Programa input_end_inicio_programa_1 (.\End__Início_do_Programa (\input_end_inicio_programa_1_end__início_do_programa ));
  Multiplexer multiplexer_1 (.in0(1'b1), .in1(1'b0), .out(Primeiro_Ciclo), .sel(register_1_q));  // open: en
  Register #(.width(1)) register_1 (.D(1'b1), .Q(register_1_q), .clk(Clock));  // open: en, clr
  Comparator #(.width(16)) comparator_1 (
    .a(PC_Atual), .b(\input_end_inicio_programa_1_end__início_do_programa ), .eq(Inicio_do_Programa));  // open: gt, lt
  Delayer delayer_1 (.\Saída (\delayer_1_saída ), .Entrada(Cache_Miss));
  Delayer delayer_2 (.\Saída (\delayer_2_saída ), .Entrada(\delayer_1_saída ));
  Delayer delayer_3 (.\Saída (\delayer_3_saída ), .Entrada(\delayer_4_saída ));
  Delayer delayer_4 (.\Saída (\delayer_4_saída ), .Entrada(\delayer_5_saída ));
  Delayer delayer_5 (.\Saída (\delayer_5_saída ), .Entrada(and_1_out));
  and and_1 (and_1_out, Clock, ~Ocorreu_Cache_Miss_Dado_Load, ~Primeiro_Ciclo);  // AND_Gate
  Register #(.width(1)) register_2 (
    .D(1'b1), .Q(Ocorreu_Cache_Miss_Dado_Load), .clk(and_2_out), .clr(and_7_out));  // open: en
  and and_2 (and_2_out, ~Clock, Cache_Miss_Load);  // AND_Gate
  Register #(.width(1)) register_3 (
    .D(1'b1), .Q(Ciclo_Posterior_ao_Cache_Miss_Dado_Load), .clk(and_3_out), .clr(and_8_out));  // open: en
  and and_3 (and_3_out, Clock, Ocorreu_Cache_Miss_Dado_Load);
  Register #(.width(1)) register_4 (.D(1'b1), .Q(Fim_do_Load), .clk(and_4_out), .clr(and_9_out));  // open: en
  and and_4 (and_4_out, ~Clock, Ciclo_Posterior_ao_Cache_Miss_Dado_Load);  // AND_Gate
  Register #(.width(1)) u_Ocorreu_Cache_Miss (
    .D(1'b1), .en(Cache_Miss), .Q(Ocorreu_Cache_Miss_t), .clk(\delayer_6_saída ), .clr(and_10_out));
  Delayer delayer_6 (.\Saída (\delayer_6_saída ), .Entrada(\delayer_2_saída ));
  Register #(.width(1)) register_5 (
    .D(1'b1), .Q(Cache_Miss___Segunda_Metade_do_Ciclo), .clk(and_5_out), .clr(and_6_out));  // open: en
  and and_5 (and_5_out, Ocorreu_Cache_Miss_t, ~Clock);  // AND_Gate
  and and_6 (and_6_out, Clock, Cache_Miss___Segunda_Metade_do_Ciclo, ~Ocorreu_Cache_Miss_t);  // AND_Gate
  Register #(.width(16)) register_6 (
    .D(\Entrada_Instrução ), .en(and_1_out), .Q(\Instrução_Buffer ), .clk(\delayer_3_saída ));  // open: clr
  and and_7 (and_7_out, Clock, Fim_do_Load);
  and and_8 (and_8_out, Ciclo_Posterior_ao_Cache_Miss_Dado_Load, ~Ocorreu_Cache_Miss_Dado_Load);  // AND_Gate
  and and_9 (and_9_out, ~Ocorreu_Cache_Miss_Dado_Load, ~Clock);  // AND_Gate
  and and_10 (and_10_out, Clock, Cache_Miss___Segunda_Metade_do_Ciclo);
  Multiplexer #(.width(16)) multiplexer_2 (
    .in0(\Entrada_Instrução ), .in1(\Instrução_Buffer ), .out(\Instrução ), .sel(or_1_out));  // open: en
  or or_1 (or_1_out, Ciclo_Posterior_ao_Store, Ocorreu_Cache_Miss_Dado_Load);
  and and_11 (Ocorreu_Cache_Miss, Ocorreu_Cache_Miss_t, ~Inicio_do_Programa);  // AND_Gate
endmodule

module Buffer_Sinais_Escrita (
  input  Clock,
  input  Clock_Fonte,
  input  Fim_do_Programa,
  input  Store,
  input  Escrita_Sub_Mem__1,
  input  Escrita_Sub_Mem__2,
  input  Escrita_Sub_Mem__3,
  input  Escrita_Sub_Mem__4,
  input  \É_Início_do_Programa ,
  input  [9:0] End__L_S_ULA,
  input  [1:0] Sub_Mem__Escrita,
  output \Escrever_Na_Memória_0 ,
  output \Escrever_Na_Memória_2 ,
  output \Escrever_Na_Memória_1 ,
  output \Escrever_Na_Memória_3 
);

  wire not_1_out, not_2_out, not_3_out, not_4_out, not_5_out, not_6_out, not_7_out, not_8_out,
       \Pré_Escrita_Sub_Mem__1 , \Pré_Escrita_Sub_Mem__2 , \Pré_Escrita_Sub_Mem__3 ,
       \Pré_Escrita_Sub_Mem__4 , register_1_q, register_2_q, register_3_q, register_4_q;
  wire [1:0] bitselector_1_out, multiplexer_1_out;

  not not_1 (not_1_out, Store);
  not not_2 (not_2_out, Clock_Fonte);
  not not_3 (not_3_out, Store);
  not not_4 (not_4_out, Clock_Fonte);
  Register #(.width(1)) register_1 (
    .D(1'b1), .en(\Pré_Escrita_Sub_Mem__1 ), .Q(register_1_q), .clk(not_2_out), .clr(not_1_out));
  Register #(.width(1)) register_2 (
    .D(1'b1), .en(\Pré_Escrita_Sub_Mem__2 ), .Q(register_2_q), .clk(not_4_out), .clr(not_3_out));
  and and_1 (\Escrever_Na_Memória_0 , register_1_q, Escrita_Sub_Mem__1, ~Clock_Fonte, ~Fim_do_Programa);  // AND_Gate
  and and_2 (\Escrever_Na_Memória_1 , register_2_q, Escrita_Sub_Mem__2, ~Clock_Fonte, ~Fim_do_Programa);  // AND_Gate
  Demultiplexer #(.select(2)) demultiplexer_1 (
    .out0(\Pré_Escrita_Sub_Mem__1 ), .out1(\Pré_Escrita_Sub_Mem__2 ), .out2(\Pré_Escrita_Sub_Mem__3 ),
    .out3(\Pré_Escrita_Sub_Mem__4 ), .in(1'b1), .sel(multiplexer_1_out));  // open: en
  Multiplexer #(.width(2)) multiplexer_1 (
    .in0(2'b00), .in1(bitselector_1_out), .out(multiplexer_1_out), .sel(Store));  // open: en
  BitSelector #(.width(10), .group(2)) bitselector_1 (.in(End__L_S_ULA), .out(bitselector_1_out), .sel(3'b000));
  Register #(.width(1)) register_3 (
    .D(1'b1), .en(\Pré_Escrita_Sub_Mem__3 ), .Q(register_3_q), .clk(not_6_out), .clr(not_5_out));
  not not_5 (not_5_out, Store);
  not not_6 (not_6_out, Clock_Fonte);
  Register #(.width(1)) register_4 (
    .D(1'b1), .en(\Pré_Escrita_Sub_Mem__4 ), .Q(register_4_q), .clk(not_8_out), .clr(not_7_out));
  not not_7 (not_7_out, Store);
  not not_8 (not_8_out, Clock_Fonte);
  and and_3 (\Escrever_Na_Memória_2 , register_3_q, Escrita_Sub_Mem__3, ~Clock_Fonte, ~Fim_do_Programa);  // AND_Gate
  and and_4 (\Escrever_Na_Memória_3 , register_4_q, Escrita_Sub_Mem__4, ~Clock_Fonte, ~Fim_do_Programa);  // AND_Gate
endmodule

module \Habilitar_Memória  (
  input  Clock,
  input  Clock_Fonte,
  input  Store,
  input  Escrita_Sub_Mem__1,
  input  Escrita_Sub_Mem__2,
  input  Escrita_Sub_Mem__3,
  input  Escrita_Sub_Mem__4,
  input  \É_início_do_Programa ,
  output \Habilitar_Memória_1 ,
  output \Habilitar_Memória_2 ,
  output \Habilitar_Memória_3 ,
  output \Habilitar_Memória_4 
);

  wire and_1_out, and_2_out, and_3_out, and_4_out, multiplexer_1_out, multiplexer_2_out, multiplexer_3_out,
       multiplexer_4_out, not_1_out, not_2_out, not_3_out, not_4_out;

  not not_1 (not_1_out, Clock_Fonte);
  Multiplexer multiplexer_1 (
    .in0(not_1_out), .in1(Clock), .out(multiplexer_1_out), .sel(\É_início_do_Programa ));  // open: en
  not not_2 (not_2_out, Clock_Fonte);
  Multiplexer multiplexer_2 (
    .in0(not_2_out), .in1(Clock), .out(multiplexer_2_out), .sel(\É_início_do_Programa ));  // open: en
  not not_3 (not_3_out, Clock_Fonte);
  Multiplexer multiplexer_3 (
    .in0(not_3_out), .in1(Clock), .out(multiplexer_3_out), .sel(\É_início_do_Programa ));  // open: en
  not not_4 (not_4_out, Clock_Fonte);
  Multiplexer multiplexer_4 (
    .in0(not_4_out), .in1(Clock), .out(multiplexer_4_out), .sel(\É_início_do_Programa ));  // open: en
  and and_1 (and_1_out, Escrita_Sub_Mem__1, multiplexer_1_out);
  and and_2 (and_2_out, Escrita_Sub_Mem__2, multiplexer_2_out);
  and and_3 (and_3_out, Escrita_Sub_Mem__3, multiplexer_3_out);
  and and_4 (and_4_out, Escrita_Sub_Mem__4, multiplexer_4_out);
  Multiplexer multiplexer_5 (.in0(1'b1), .in1(and_1_out), .out(\Habilitar_Memória_1 ), .sel(Store));  // open: en
  Multiplexer multiplexer_6 (.in0(1'b1), .in1(and_2_out), .out(\Habilitar_Memória_2 ), .sel(Store));  // open: en
  Multiplexer multiplexer_7 (.in0(1'b1), .in1(and_3_out), .out(\Habilitar_Memória_3 ), .sel(Store));  // open: en
  Multiplexer multiplexer_8 (.in0(1'b1), .in1(and_4_out), .out(\Habilitar_Memória_4 ), .sel(Store));  // open: en
endmodule

module \Calcular_Endereço  (
  input  [9:0] End__L_S_ULA,
  input  [9:0] End__PC,
  input  Cache_Miss_Load,
  input  Escrever_Dados,
  input  Primeiro_Ciclo,
  input  Store,
  input  Load,
  input  Pre_store,
  output [9:0] Numero_do_Bloco,
  output [9:0] \Sub_Memória 
);

  wire and_1_out, or_1_out;
  wire [9:0] End__Final, multiplexer_2_out;

  Multiplexer #(.width(10)) multiplexer_1 (
    .in0(multiplexer_2_out), .in1(End__PC), .out(End__Final), .sel(and_1_out));  // open: en
  and and_1 (and_1_out, ~Cache_Miss_Load, Primeiro_Ciclo);  // AND_Gate
  Multiplexer #(.width(10), .enable("false")) multiplexer_2 (
    .in0(End__PC), .in1(End__L_S_ULA), .out(multiplexer_2_out), .sel(or_1_out));
  or or_1 (or_1_out, Load, Store, Cache_Miss_Load, Pre_store);
  Divider #(.width(10)) divider_1 (
    .a(End__Final), .b(10'h4), .out(Numero_do_Bloco), .rem(\Sub_Memória ));  // open: upper
endmodule

module Delayer (
  input  Entrada,
  output \Saída 
);

  wire not_1_out, not_2_out, not_4_out, not_5_out, not_6_out, not_7_out, not_8_out, not_9_out, not_10_out,
       not_11_out, not_12_out;

  not not_1 (not_1_out, not_7_out);
  not not_2 (not_2_out, not_1_out);
  not not_3 (\Saída , not_2_out);
  not not_4 (not_4_out, not_5_out);
  not not_5 (not_5_out, not_6_out);
  not not_6 (not_6_out, not_11_out);
  not not_7 (not_7_out, not_4_out);
  not not_8 (not_8_out, not_12_out);
  not not_9 (not_9_out, not_8_out);
  not not_10 (not_10_out, not_9_out);
  not not_11 (not_11_out, not_10_out);
  not not_12 (not_12_out, Entrada);
endmodule

module Direcionar_Dados_Entrada_MP (
  input  Escrever_Dados,
  input  [9:0] \Sub_Memória ,
  input  [15:0] Entrada_Dado_a_ser_Escrito,
  input  Store,
  output [15:0] Entrada_1,
  output [15:0] Entrada_2,
  output [15:0] Entrada_3,
  output [15:0] Entrada_4,
  output Escrita_Sub_Mem__1,
  output Escrita_Sub_Mem__2,
  output Escrita_Sub_Mem__3,
  output Escrita_Sub_Mem__4,
  output [1:0] Sub_Mem__Escrita
);

  wire demultiplexer_1_out0, demultiplexer_1_out1, demultiplexer_1_out2, demultiplexer_1_out3;
  wire [1:0] multiplexer_1_out;

  BitSelector #(.width(10), .group(2)) bitselector_1 (.in(\Sub_Memória ), .out(Sub_Mem__Escrita), .sel(3'b000));
  Demultiplexer #(.select(2)) demultiplexer_1 (
    .out0(demultiplexer_1_out0), .out1(demultiplexer_1_out1), .out2(demultiplexer_1_out2),
    .out3(demultiplexer_1_out3), .in(1'b1), .sel(multiplexer_1_out));  // open: en
  Multiplexer #(.width(2)) multiplexer_1 (
    .in0(2'b00), .in1(Sub_Mem__Escrita), .out(multiplexer_1_out), .sel(Store));  // open: en
  Demultiplexer #(.select(2), .width(16)) demultiplexer_2 (
    .out0(Entrada_1), .out1(Entrada_2), .out2(Entrada_3), .out3(Entrada_4), .in(Entrada_Dado_a_ser_Escrito),
    .sel(Sub_Mem__Escrita));  // open: en
  and and_1 (Escrita_Sub_Mem__1, Escrever_Dados, demultiplexer_1_out0);
  and and_2 (Escrita_Sub_Mem__2, demultiplexer_1_out1, Escrever_Dados);
  and and_3 (Escrita_Sub_Mem__3, demultiplexer_1_out2, Escrever_Dados);
  and and_4 (Escrita_Sub_Mem__4, demultiplexer_1_out3, Escrever_Dados);
endmodule

module Store_Handler (
  input  Store,
  input  Clock,
  output Ciclo_Posterior_ao_Store,
  output \Pré_store 
);

  wire and_1_out, and_2_out, and_3_out, and_4_out, and_5_out, and_6_out, Baixa_do_Primeiro_Ciclo_Store_q,
       Baixa_Do_Segundo_Ciclo_Store_q, \delayer_1_saída , \delayer_2_saída , \delayer_3_saída ,
       \delayer_4_saída , \delayer_5_saída , \delayer_6_saída ;

  and and_1 (and_1_out, Store, Clock);
  and and_2 (and_2_out, and_1_out, Store);
  Delayer delayer_1 (.\Saída (\delayer_1_saída ), .Entrada(\delayer_2_saída ));
  Delayer delayer_2 (.\Saída (\delayer_2_saída ), .Entrada(and_2_out));
  Register #(.width(1)) register_1 (
    .D(1'b1), .en(and_2_out), .Q(\Pré_store ), .clk(\delayer_3_saída ), .clr(and_6_out));
  Delayer delayer_3 (.\Saída (\delayer_3_saída ), .Entrada(\delayer_1_saída ));
  Register #(.width(1)) Baixa_do_Primeiro_Ciclo_Store (
    .D(1'b1), .Q(Baixa_do_Primeiro_Ciclo_Store_q), .clk(and_3_out), .clr(and_6_out));  // open: en
  and and_3 (and_3_out, \Pré_store , ~Clock);  // AND_Gate
  Register #(.width(1)) register_2 (
    .D(1'b1), .Q(Ciclo_Posterior_ao_Store), .clk(and_4_out), .clr(and_6_out));  // open: en
  and and_4 (and_4_out, Baixa_do_Primeiro_Ciclo_Store_q, Clock);
  and and_5 (and_5_out, Ciclo_Posterior_ao_Store, ~Clock);  // AND_Gate
  Register #(.width(1)) Baixa_Do_Segundo_Ciclo_Store (
    .D(1'b1), .Q(Baixa_Do_Segundo_Ciclo_Store_q), .clk(and_5_out), .clr(\delayer_4_saída ));  // open: en
  Delayer delayer_4 (.\Saída (\delayer_4_saída ), .Entrada(\delayer_5_saída ));
  Delayer delayer_5 (.\Saída (\delayer_5_saída ), .Entrada(\delayer_6_saída ));
  Delayer delayer_6 (.\Saída (\delayer_6_saída ), .Entrada(and_6_out));
  and and_6 (and_6_out, Baixa_Do_Segundo_Ciclo_Store_q, Clock);
endmodule

module Buffer_Store (
  input  Clock,
  input  Ciclo_Posterior_ao_Store,
  input  Pre_store,
  input  [15:0] Entrada_Mem__1,
  input  [15:0] Entrada_Mem__3,
  input  [1:0] Palavra_L_S,
  input  [15:0] Dado_Store,
  input  [15:0] Entrada_Mem__2,
  input  [15:0] Entrada_Mem__4,
  output [15:0] Entrada_1,
  output [15:0] Entrada_3,
  output [15:0] Entrada_2,
  output [15:0] Entrada_4
);

  wire and_1_out, and_2_out, and_3_out, \delayer_1_saída , \delayer_2_saída , \delayer_3_saída ,
       demultiplexer_1_out0, demultiplexer_1_out1, demultiplexer_1_out2, demultiplexer_1_out3;
  wire [15:0] Entrada_Dado_Buffer_Store_1, Entrada_Dado_Buffer_Store_2, Entrada_Dado_Buffer_Store_3,
       Entrada_Dado_Buffer_Store_4, \Saída_Store_1 , \Saída_Store_2 , \Saída_Store_3 , \Saída_Store_4 ;

  and and_1 (and_1_out, ~Ciclo_Posterior_ao_Store, Pre_store);  // AND_Gate
  Demultiplexer #(.select(2)) demultiplexer_1 (
    .out0(demultiplexer_1_out0), .out1(demultiplexer_1_out1), .out2(demultiplexer_1_out2),
    .out3(demultiplexer_1_out3), .in(and_1_out), .sel(Palavra_L_S));  // open: en
  Multiplexer #(.width(16)) multiplexer_1 (
    .in0(Entrada_Mem__1), .in1(Dado_Store), .out(Entrada_Dado_Buffer_Store_1), .sel(demultiplexer_1_out0));  // open: en
  Multiplexer #(.width(16)) multiplexer_2 (
    .in0(Entrada_Mem__2), .in1(Dado_Store), .out(Entrada_Dado_Buffer_Store_2), .sel(demultiplexer_1_out1));  // open: en
  Multiplexer #(.width(16)) multiplexer_3 (
    .in0(Entrada_Mem__3), .in1(Dado_Store), .out(Entrada_Dado_Buffer_Store_3), .sel(demultiplexer_1_out2));  // open: en
  Multiplexer #(.width(16)) multiplexer_4 (
    .in0(Entrada_Mem__4), .in1(Dado_Store), .out(Entrada_Dado_Buffer_Store_4), .sel(demultiplexer_1_out3));  // open: en
  and and_2 (and_2_out, Pre_store, ~Clock);  // AND_Gate
  Delayer delayer_1 (.\Saída (\delayer_1_saída ), .Entrada(\delayer_2_saída ));
  Delayer delayer_2 (.\Saída (\delayer_2_saída ), .Entrada(\delayer_3_saída ));
  Delayer delayer_3 (.\Saída (\delayer_3_saída ), .Entrada(and_3_out));
  and and_3 (and_3_out, and_2_out, ~Ciclo_Posterior_ao_Store);  // AND_Gate
  Register #(.width(16)) register_1 (
    .D(Entrada_Dado_Buffer_Store_1), .en(and_3_out), .Q(\Saída_Store_1 ), .clk(\delayer_1_saída ));  // open: clr
  Register #(.width(16)) register_2 (
    .D(Entrada_Dado_Buffer_Store_2), .en(and_3_out), .Q(\Saída_Store_2 ), .clk(\delayer_1_saída ));  // open: clr
  Register #(.width(16)) register_3 (
    .D(Entrada_Dado_Buffer_Store_3), .en(and_3_out), .Q(\Saída_Store_3 ), .clk(\delayer_1_saída ));  // open: clr
  Register #(.width(16)) register_4 (
    .D(Entrada_Dado_Buffer_Store_4), .en(and_3_out), .Q(\Saída_Store_4 ), .clk(\delayer_1_saída ));  // open: clr
  Multiplexer #(.width(16)) multiplexer_5 (
    .in0(Entrada_Mem__1), .in1(\Saída_Store_1 ), .out(Entrada_1), .sel(Ciclo_Posterior_ao_Store));  // open: en
  Multiplexer #(.width(16)) multiplexer_6 (
    .in0(Entrada_Mem__2), .in1(\Saída_Store_2 ), .out(Entrada_2), .sel(Ciclo_Posterior_ao_Store));  // open: en
  Multiplexer #(.width(16)) multiplexer_7 (
    .in0(Entrada_Mem__3), .in1(\Saída_Store_3 ), .out(Entrada_3), .sel(Ciclo_Posterior_ao_Store));  // open: en
  Multiplexer #(.width(16)) multiplexer_8 (
    .in0(Entrada_Mem__4), .in1(\Saída_Store_4 ), .out(Entrada_4), .sel(Ciclo_Posterior_ao_Store));  // open: en
endmodule

module Persistir_Sinal_Escrita_Cache_Direta (
  input  in_1,
  input  in_2,
  output out_3
);

  wire and_1_out, and_2_out, and_3_out, and_4_out, and_5_out, and_6_out, \delayer_1_saída ,
       \delayer_2_saída , \delayer_3_saída , \delayer_4_saída , \delayer_5_saída , \delayer_6_saída ,
       \delayer_7_saída , \delayer_8_saída , \delayer_9_saída , \delayer_10_saída , \delayer_11_saída ,
       \delayer_12_saída , \delayer_13_saída , register_2_q;

  and and_1 (and_1_out, in_2, in_1);
  Delayer delayer_1 (.\Saída (\delayer_1_saída ), .Entrada(and_1_out));
  and and_2 (and_2_out, \delayer_1_saída , in_2);
  Delayer delayer_2 (.\Saída (\delayer_2_saída ), .Entrada(and_2_out));
  Delayer delayer_3 (.\Saída (\delayer_3_saída ), .Entrada(\delayer_4_saída ));
  Delayer delayer_4 (.\Saída (\delayer_4_saída ), .Entrada(\delayer_2_saída ));
  and and_3 (and_3_out, in_1, and_4_out, \delayer_13_saída );
  and and_4 (and_4_out, ~in_2, out_3);  // AND_Gate
  Register #(.width(1)) register_1 (.D(1'b1), .en(and_1_out), .Q(out_3), .clk(\delayer_3_saída ), .clr(and_3_out));
  and and_5 (and_5_out, out_3, ~\delayer_5_saída );  // AND_Gate
  Delayer delayer_5 (.\Saída (\delayer_5_saída ), .Entrada(in_1));
  Delayer delayer_6 (.\Saída (\delayer_6_saída ), .Entrada(\delayer_9_saída ));
  Delayer delayer_7 (.\Saída (\delayer_7_saída ), .Entrada(\delayer_8_saída ));
  Delayer delayer_8 (.\Saída (\delayer_8_saída ), .Entrada(\delayer_10_saída ));
  Delayer delayer_9 (.\Saída (\delayer_9_saída ), .Entrada(\delayer_11_saída ));
  Delayer delayer_10 (.\Saída (\delayer_10_saída ), .Entrada(\delayer_6_saída ));
  Delayer delayer_11 (.\Saída (\delayer_11_saída ), .Entrada(and_6_out));
  Register #(.width(1)) register_2 (.D(1'b1), .Q(register_2_q), .clk(and_5_out), .clr(\delayer_7_saída ));  // open: en
  Delayer delayer_12 (.\Saída (\delayer_12_saída ), .Entrada(register_2_q));
  Delayer delayer_13 (.\Saída (\delayer_13_saída ), .Entrada(\delayer_12_saída ));
  and and_6 (and_6_out, \delayer_5_saída , \delayer_13_saída );

  // Other names for the same wires on the sheet: Clock = in_1; Escrita = in_2; escrita_persistida = out_3
endmodule

module \Início_do_Programa_Handler  (
  input  [15:0] \Endereço_from_PC ,
  input  Clock_Fonte,
  input  Escrever_Bloco_Load,
  output \Enable_Válido_e_TAG ,
  output \Clock_Válido_e_TAG ,
  output Clock,
  output \Início_Prog 
);

  wire and_1_out, gerenciador_clock_inicial_1_clock_inicial, not_1_out;
  wire [15:0] \input_end_inicio_programa_1_end__início_do_programa ;

  Multiplexer multiplexer_1 (.in0(Clock), .in1(1'b0), .out(\Enable_Válido_e_TAG ), .sel(\Início_Prog ));  // open: en
  Multiplexer multiplexer_2 (
    .in0(Clock), .in1(not_1_out), .out(\Clock_Válido_e_TAG ), .sel(\Início_Prog ));  // open: en
  not not_1 (not_1_out, Clock);
  Input_End__Inicio_Programa input_end_inicio_programa_1 (.\End__Início_do_Programa (\input_end_inicio_programa_1_end__início_do_programa ));
  Comparator #(.width(16)) comparator_1 (
    .a(\Endereço_from_PC ), .b(\input_end_inicio_programa_1_end__início_do_programa ), .eq(\Início_Prog ));  // open: gt, lt
  Multiplexer multiplexer_3 (
    .in0(gerenciador_clock_inicial_1_clock_inicial), .in1(Clock_Fonte), .out(Clock), .sel(and_1_out));  // open: en
  and and_1 (and_1_out, Escrever_Bloco_Load, Clock_Fonte);
  Gerenciador_Clock_Inicial gerenciador_clock_inicial_1 (
    .Clock_Inicial(gerenciador_clock_inicial_1_clock_inicial), .Clock(Clock_Fonte),
    .PC_Atual(\Endereço_from_PC ));
endmodule

module \Verificar_se_O_Bloco_Está_na_Cache  (
  input  [4:0] TAG_Linha_0,
  input  [4:0] TAG_Linha_1,
  input  [4:0] TAG_Linha_2,
  input  [4:0] TAG_Linha_3,
  input  [4:0] TAG_Linha_4,
  input  [4:0] TAG_Linha_5,
  input  [4:0] TAG_Linha_6,
  input  [4:0] TAG_Linha_7,
  input  [4:0] TAG,
  input  [2:0] Linha,
  input  [4:0] TAG__L_S,
  input  [2:0] Linha__L_S,
  input  Load,
  output Bloco_Com_a_Instrucao_esta_na_cache,
  output Bloco_Com_o_dado_do_Load_esta_na_cache
);

  wire comparator_2_eq;
  wire [4:0] multiplexer_1_out, multiplexer_2_out;

  Multiplexer #(.select(3), .width(5)) multiplexer_1 (
    .in0(TAG_Linha_0), .in1(TAG_Linha_1), .in2(TAG_Linha_2), .in3(TAG_Linha_3), .in4(TAG_Linha_4),
    .in5(TAG_Linha_5), .in6(TAG_Linha_6), .in7(TAG_Linha_7), .out(multiplexer_1_out), .sel(Linha));  // open: en
  Multiplexer #(.select(3), .width(5)) multiplexer_2 (
    .in0(TAG_Linha_0), .in1(TAG_Linha_1), .in2(TAG_Linha_2), .in3(TAG_Linha_3), .in4(TAG_Linha_4),
    .in5(TAG_Linha_5), .in6(TAG_Linha_6), .in7(TAG_Linha_7), .out(multiplexer_2_out), .sel(Linha__L_S));  // open: en
  Comparator #(.width(5)) comparator_1 (
    .a(multiplexer_1_out), .b(TAG), .eq(Bloco_Com_a_Instrucao_esta_na_cache));  // open: gt, lt
  Multiplexer multiplexer_3 (
    .in0(1'b1), .in1(comparator_2_eq), .out(Bloco_Com_o_dado_do_Load_esta_na_cache), .sel(Load));  // open: en
  Comparator #(.width(5)) comparator_2 (.a(multiplexer_2_out), .b(TAG__L_S), .eq(comparator_2_eq));  // open: gt, lt
endmodule

module \Verificar_se_a_Linha_é_Válida  (
  input  \Válido_Linha_0 ,
  input  \Válido_Linha_1 ,
  input  \Válido_Linha_2 ,
  input  \Válido_Linha_3 ,
  input  \Válido_Linha_4 ,
  input  \Válido_Linha_5 ,
  input  \Válido_Linha_6 ,
  input  \Válido_Linha_7 ,
  input  [2:0] Linha,
  input  [2:0] Linha__L_S,
  output \Válido_Linha_Instrucao ,
  output \Válido_Linha_com_dado_Load 
);

  Multiplexer #(.select(3)) multiplexer_1 (
    .in0(\Válido_Linha_0 ), .in1(\Válido_Linha_1 ), .in2(\Válido_Linha_2 ), .in3(\Válido_Linha_3 ),
    .in4(\Válido_Linha_4 ), .in5(\Válido_Linha_5 ), .in6(\Válido_Linha_6 ), .in7(\Válido_Linha_7 ),
    .out(\Válido_Linha_com_dado_Load ), .sel(Linha__L_S));  // open: en
  Multiplexer #(.select(3)) multiplexer_2 (
    .in0(\Válido_Linha_0 ), .in1(\Válido_Linha_1 ), .in2(\Válido_Linha_2 ), .in3(\Válido_Linha_3 ),
    .in4(\Válido_Linha_4 ), .in5(\Válido_Linha_5 ), .in6(\Válido_Linha_6 ), .in7(\Válido_Linha_7 ),
    .out(\Válido_Linha_Instrucao ), .sel(Linha));  // open: en
endmodule

module Linha_de_Escrita_Handler (
  input  Escrever_Bloco_Load,
  input  Load,
  input  [2:0] Linha__L_S,
  input  Clock,
  input  Escrita,
  input  \Início_Prog ,
  input  [2:0] Linha,
  input  Ciclo_Posterior_ao_Store,
  output Escrita_Linha_0,
  output Escrita_Linha_4,
  output Escrita_Linha_1,
  output Escrita_Linha_5,
  output Escrita_Linha_2,
  output Escrita_Linha_6,
  output Escrita_Linha_3,
  output Escrita_Linha_7
);

  wire \Instrução_Escrita_Linha_0 , \Instrução_Escrita_Linha_1 , \Instrução_Escrita_Linha_2 ,
       \Instrução_Escrita_Linha_3 , \Instrução_Escrita_Linha_4 , \Instrução_Escrita_Linha_5 ,
       \Instrução_Escrita_Linha_6 , \Instrução_Escrita_Linha_7 , Load_Escrita_Linha_0, Load_Escrita_Linha_1,
       Load_Escrita_Linha_2, Load_Escrita_Linha_3, Load_Escrita_Linha_4, Load_Escrita_Linha_5,
       Load_Escrita_Linha_6, Load_Escrita_Linha_7, multiplexer_1_out, multiplexer_2_out, multiplexer_4_out,
       multiplexer_5_out, multiplexer_6_out, multiplexer_7_out, multiplexer_8_out, multiplexer_9_out,
       multiplexer_10_out, multiplexer_11_out, persistir_sinal_escrita_cache_direta_1_out_3;
  wire [2:0] multiplexer_3_out;

  Multiplexer multiplexer_1 (.in0(1'b0), .in1(Escrever_Bloco_Load), .out(multiplexer_1_out), .sel(Load));  // open: en
  Multiplexer multiplexer_2 (
    .in0(persistir_sinal_escrita_cache_direta_1_out_3), .in1(1'b1), .out(multiplexer_2_out),
    .sel(\Início_Prog ));  // open: en
  Demultiplexer #(.select(3)) demultiplexer_1 (
    .out0(Load_Escrita_Linha_0), .out1(Load_Escrita_Linha_1), .out2(Load_Escrita_Linha_2),
    .out3(Load_Escrita_Linha_3), .out4(Load_Escrita_Linha_4), .out5(Load_Escrita_Linha_5),
    .out6(Load_Escrita_Linha_6), .out7(Load_Escrita_Linha_7), .in(multiplexer_1_out), .sel(Linha__L_S));  // open: en
  Persistir_Sinal_Escrita_Cache_Direta persistir_sinal_escrita_cache_direta_1 (
    .in_2(Escrita), .in_1(Clock), .out_3(persistir_sinal_escrita_cache_direta_1_out_3));
  Demultiplexer #(.select(3)) demultiplexer_2 (
    .out0(\Instrução_Escrita_Linha_0 ), .out1(\Instrução_Escrita_Linha_1 ),
    .out2(\Instrução_Escrita_Linha_2 ), .out3(\Instrução_Escrita_Linha_3 ),
    .out4(\Instrução_Escrita_Linha_4 ), .out5(\Instrução_Escrita_Linha_5 ),
    .out6(\Instrução_Escrita_Linha_6 ), .out7(\Instrução_Escrita_Linha_7 ), .in(multiplexer_2_out),
    .sel(multiplexer_3_out));  // open: en
  Multiplexer #(.width(3)) multiplexer_3 (
    .in0(Linha), .in1(Linha__L_S), .out(multiplexer_3_out), .sel(Ciclo_Posterior_ao_Store));  // open: en
  Multiplexer multiplexer_4 (
    .in0(1'b0), .in1(Load_Escrita_Linha_0), .out(multiplexer_4_out), .sel(Escrever_Bloco_Load));  // open: en
  Multiplexer multiplexer_5 (
    .in0(1'b0), .in1(Load_Escrita_Linha_1), .out(multiplexer_5_out), .sel(Escrever_Bloco_Load));  // open: en
  Multiplexer multiplexer_6 (
    .in0(1'b0), .in1(Load_Escrita_Linha_2), .out(multiplexer_6_out), .sel(Escrever_Bloco_Load));  // open: en
  Multiplexer multiplexer_7 (
    .in0(1'b0), .in1(Load_Escrita_Linha_3), .out(multiplexer_7_out), .sel(Escrever_Bloco_Load));  // open: en
  or or_1 (Escrita_Linha_0, \Instrução_Escrita_Linha_0 , multiplexer_4_out);
  or or_2 (Escrita_Linha_1, \Instrução_Escrita_Linha_1 , multiplexer_5_out);
  or or_3 (Escrita_Linha_2, \Instrução_Escrita_Linha_2 , multiplexer_6_out);
  or or_4 (Escrita_Linha_3, \Instrução_Escrita_Linha_3 , multiplexer_7_out);
  Multiplexer multiplexer_8 (
    .in0(1'b0), .in1(Load_Escrita_Linha_4), .out(multiplexer_8_out), .sel(Escrever_Bloco_Load));  // open: en
  Multiplexer multiplexer_9 (
    .in0(1'b0), .in1(Load_Escrita_Linha_5), .out(multiplexer_9_out), .sel(Escrever_Bloco_Load));  // open: en
  Multiplexer multiplexer_10 (
    .in0(1'b0), .in1(Load_Escrita_Linha_6), .out(multiplexer_10_out), .sel(Escrever_Bloco_Load));  // open: en
  Multiplexer multiplexer_11 (
    .in0(1'b0), .in1(Load_Escrita_Linha_7), .out(multiplexer_11_out), .sel(Escrever_Bloco_Load));  // open: en
  or or_5 (Escrita_Linha_4, \Instrução_Escrita_Linha_4 , multiplexer_8_out);
  or or_6 (Escrita_Linha_5, \Instrução_Escrita_Linha_5 , multiplexer_9_out);
  or or_7 (Escrita_Linha_6, \Instrução_Escrita_Linha_6 , multiplexer_10_out);
  or or_8 (Escrita_Linha_7, \Instrução_Escrita_Linha_7 , multiplexer_11_out);
endmodule

module Clock_Fim_Programa (
  input  Clock_Fonte,
  input  Fim_do_Programa,
  output Clock
);

  Multiplexer multiplexer_1 (.in0(Clock_Fonte), .in1(1'b1), .out(Clock), .sel(Fim_do_Programa));  // open: en
endmodule
